// Logisim project Conway's Game of Life.circ as structural Verilog: 10 circuits, main circuit Main
module Main (
  input  Run__Attivare_Ticks_prima,
  output [31:0] out_2
);

  wire button_1_out, button_2_out, button_3_out, button_4_out, button_5_out, button_6_out, button_7_out,
       button_8_out, button_9_out, button_10_out, button_11_out, button_12_out, button_13_out, button_14_out,
       button_15_out, button_16_out, button_17_out, button_18_out, button_19_out, button_20_out,
       button_21_out, button_22_out, button_23_out, button_24_out, button_25_out, button_26_out,
       button_27_out, button_28_out, button_29_out, button_30_out, button_31_out, button_32_out,
       button_33_out, button_34_out, button_35_out, button_36_out, button_37_out, button_38_out,
       button_39_out, button_40_out, button_41_out, button_42_out, button_43_out, button_44_out,
       button_45_out, button_46_out, button_47_out, button_48_out, button_49_out, button_50_out,
       button_51_out, button_52_out, button_53_out, button_54_out, button_55_out, button_56_out,
       button_57_out, button_58_out, button_59_out, button_60_out, button_61_out, button_62_out,
       button_63_out, button_64_out, button_65_out, button_66_out, button_67_out, button_68_out,
       button_69_out, button_70_out, button_71_out, button_72_out, button_73_out, button_74_out,
       button_75_out, button_76_out, button_77_out, button_78_out, button_79_out, button_80_out,
       button_81_out, button_82_out, button_83_out, button_84_out, button_85_out, button_86_out,
       button_87_out, button_88_out, button_89_out, button_90_out, button_91_out, button_92_out,
       button_93_out, button_94_out, button_95_out, button_96_out, button_97_out, button_98_out,
       button_99_out, button_100_out, button_101_out, button_102_out, button_103_out, button_104_out,
       button_105_out, button_106_out, button_107_out, button_108_out, button_109_out, button_110_out,
       button_111_out, button_112_out, button_113_out, button_114_out, button_115_out, button_116_out,
       button_117_out, button_118_out, button_119_out, button_120_out, button_121_out, button_122_out,
       button_123_out, button_124_out, button_125_out, button_126_out, button_127_out, button_128_out,
       button_129_out, button_130_out, button_131_out, button_132_out, button_133_out, button_134_out,
       button_135_out, button_136_out, button_137_out, button_138_out, button_139_out, button_140_out,
       button_141_out, button_142_out, button_143_out, button_144_out, button_145_out, button_146_out,
       button_147_out, button_148_out, button_149_out, button_150_out, button_151_out, button_152_out,
       button_153_out, button_154_out, button_155_out, button_156_out, button_157_out, button_158_out,
       button_159_out, button_160_out, button_161_out, button_162_out, button_163_out, button_164_out,
       button_165_out, button_166_out, button_167_out, button_168_out, button_169_out, button_170_out,
       button_171_out, button_172_out, button_173_out, button_174_out, button_175_out, button_176_out,
       button_177_out, button_178_out, button_179_out, button_180_out, button_181_out, button_182_out,
       button_183_out, button_184_out, button_185_out, button_186_out, button_187_out, button_188_out,
       button_189_out, button_190_out, button_191_out, button_192_out, button_193_out, button_194_out,
       button_195_out, button_196_out, button_197_out, button_198_out, button_199_out, button_200_out,
       button_201_out, button_202_out, button_203_out, button_204_out, button_205_out, button_206_out,
       button_207_out, button_208_out, button_209_out, button_210_out, button_211_out, button_212_out,
       button_213_out, button_214_out, button_215_out, button_216_out, button_217_out, button_218_out,
       button_219_out, button_220_out, button_221_out, button_222_out, button_223_out, button_224_out,
       button_225_out, clock_1_out_3, setresetcounter_1_out_16, Step_out;
  wire [14:0] force_l_utente_cambia_i_bit_1_out_17, force_l_utente_cambia_i_bit_1_out_18,
       force_l_utente_cambia_i_bit_1_out_19, force_l_utente_cambia_i_bit_1_out_20,
       force_l_utente_cambia_i_bit_1_out_21, force_l_utente_cambia_i_bit_1_out_22,
       force_l_utente_cambia_i_bit_1_out_23, force_l_utente_cambia_i_bit_1_out_24,
       force_l_utente_cambia_i_bit_1_out_25, force_l_utente_cambia_i_bit_1_out_26,
       force_l_utente_cambia_i_bit_1_out_27, force_l_utente_cambia_i_bit_1_out_28,
       force_l_utente_cambia_i_bit_1_out_29, force_l_utente_cambia_i_bit_1_out_30,
       force_l_utente_cambia_i_bit_1_out_31, inputrow_1_out_16, inputrow_2_out_16, inputrow_3_out_16,
       inputrow_4_out_16, inputrow_5_out_16, inputrow_6_out_16, inputrow_7_out_16, inputrow_8_out_16,
       inputrow_9_out_16, inputrow_10_out_16, inputrow_11_out_16, inputrow_12_out_16, inputrow_13_out_16,
       inputrow_14_out_16, inputrow_15_out_16;
  wire [31:0] Counter_q;

  Button button_1 (.out(button_1_out));
  Button button_2 (.out(button_2_out));
  Button button_3 (.out(button_3_out));
  Button button_4 (.out(button_4_out));
  Button button_5 (.out(button_5_out));
  Button button_6 (.out(button_6_out));
  Button button_7 (.out(button_7_out));
  Button button_8 (.out(button_8_out));
  Button button_9 (.out(button_9_out));
  Button button_10 (.out(button_10_out));
  Button button_11 (.out(button_11_out));
  Button button_12 (.out(button_12_out));
  Button button_13 (.out(button_13_out));
  Button button_14 (.out(button_14_out));
  Button button_15 (.out(button_15_out));
  Button button_16 (.out(button_16_out));
  Button button_17 (.out(button_17_out));
  Button button_18 (.out(button_18_out));
  Button button_19 (.out(button_19_out));
  Button button_20 (.out(button_20_out));
  Button button_21 (.out(button_21_out));
  Button button_22 (.out(button_22_out));
  Button button_23 (.out(button_23_out));
  Button button_24 (.out(button_24_out));
  Button button_25 (.out(button_25_out));
  Button button_26 (.out(button_26_out));
  Button button_27 (.out(button_27_out));
  Button button_28 (.out(button_28_out));
  Button button_29 (.out(button_29_out));
  Button button_30 (.out(button_30_out));
  Button button_31 (.out(button_31_out));
  Button button_32 (.out(button_32_out));
  Button button_33 (.out(button_33_out));
  Button button_34 (.out(button_34_out));
  Button button_35 (.out(button_35_out));
  Button button_36 (.out(button_36_out));
  Button button_37 (.out(button_37_out));
  Button button_38 (.out(button_38_out));
  Button button_39 (.out(button_39_out));
  Button button_40 (.out(button_40_out));
  Button button_41 (.out(button_41_out));
  Button button_42 (.out(button_42_out));
  Button button_43 (.out(button_43_out));
  Button button_44 (.out(button_44_out));
  Button button_45 (.out(button_45_out));
  Button button_46 (.out(button_46_out));
  Button button_47 (.out(button_47_out));
  Button button_48 (.out(button_48_out));
  Button button_49 (.out(button_49_out));
  Button button_50 (.out(button_50_out));
  Button button_51 (.out(button_51_out));
  Button button_52 (.out(button_52_out));
  Button button_53 (.out(button_53_out));
  Button button_54 (.out(button_54_out));
  Button button_55 (.out(button_55_out));
  Button button_56 (.out(button_56_out));
  Button button_57 (.out(button_57_out));
  Button button_58 (.out(button_58_out));
  Button button_59 (.out(button_59_out));
  Button button_60 (.out(button_60_out));
  Button button_61 (.out(button_61_out));
  Button button_62 (.out(button_62_out));
  Button button_63 (.out(button_63_out));
  Button button_64 (.out(button_64_out));
  Button button_65 (.out(button_65_out));
  Button button_66 (.out(button_66_out));
  Button button_67 (.out(button_67_out));
  Button button_68 (.out(button_68_out));
  Button button_69 (.out(button_69_out));
  Button button_70 (.out(button_70_out));
  Button button_71 (.out(button_71_out));
  Button button_72 (.out(button_72_out));
  Button button_73 (.out(button_73_out));
  Button button_74 (.out(button_74_out));
  Button button_75 (.out(button_75_out));
  Button button_76 (.out(button_76_out));
  Button button_77 (.out(button_77_out));
  Button button_78 (.out(button_78_out));
  Button button_79 (.out(button_79_out));
  Button button_80 (.out(button_80_out));
  Button button_81 (.out(button_81_out));
  Button button_82 (.out(button_82_out));
  Button button_83 (.out(button_83_out));
  Button button_84 (.out(button_84_out));
  Button button_85 (.out(button_85_out));
  Button button_86 (.out(button_86_out));
  Button button_87 (.out(button_87_out));
  Button button_88 (.out(button_88_out));
  Button button_89 (.out(button_89_out));
  Button button_90 (.out(button_90_out));
  Button button_91 (.out(button_91_out));
  Button button_92 (.out(button_92_out));
  Button button_93 (.out(button_93_out));
  Button button_94 (.out(button_94_out));
  Button button_95 (.out(button_95_out));
  Button button_96 (.out(button_96_out));
  Button button_97 (.out(button_97_out));
  Button button_98 (.out(button_98_out));
  Button button_99 (.out(button_99_out));
  Button button_100 (.out(button_100_out));
  Button button_101 (.out(button_101_out));
  Button button_102 (.out(button_102_out));
  Button button_103 (.out(button_103_out));
  Button button_104 (.out(button_104_out));
  Button button_105 (.out(button_105_out));
  Button button_106 (.out(button_106_out));
  Button button_107 (.out(button_107_out));
  Button button_108 (.out(button_108_out));
  Button button_109 (.out(button_109_out));
  Button button_110 (.out(button_110_out));
  Button button_111 (.out(button_111_out));
  Button button_112 (.out(button_112_out));
  Button button_113 (.out(button_113_out));
  Button button_114 (.out(button_114_out));
  Button button_115 (.out(button_115_out));
  Button button_116 (.out(button_116_out));
  Button button_117 (.out(button_117_out));
  Button button_118 (.out(button_118_out));
  Button button_119 (.out(button_119_out));
  Button button_120 (.out(button_120_out));
  Button button_121 (.out(button_121_out));
  Button button_122 (.out(button_122_out));
  Button button_123 (.out(button_123_out));
  Button button_124 (.out(button_124_out));
  Button button_125 (.out(button_125_out));
  Button button_126 (.out(button_126_out));
  Button button_127 (.out(button_127_out));
  Button button_128 (.out(button_128_out));
  Button button_129 (.out(button_129_out));
  Button button_130 (.out(button_130_out));
  Button button_131 (.out(button_131_out));
  Button button_132 (.out(button_132_out));
  Button button_133 (.out(button_133_out));
  Button button_134 (.out(button_134_out));
  Button button_135 (.out(button_135_out));
  Button button_136 (.out(button_136_out));
  Button button_137 (.out(button_137_out));
  Button button_138 (.out(button_138_out));
  Button button_139 (.out(button_139_out));
  Button button_140 (.out(button_140_out));
  Button button_141 (.out(button_141_out));
  Button button_142 (.out(button_142_out));
  Button button_143 (.out(button_143_out));
  Button button_144 (.out(button_144_out));
  Button button_145 (.out(button_145_out));
  Button button_146 (.out(button_146_out));
  Button button_147 (.out(button_147_out));
  Button button_148 (.out(button_148_out));
  Button button_149 (.out(button_149_out));
  Button button_150 (.out(button_150_out));
  Button button_151 (.out(button_151_out));
  Button button_152 (.out(button_152_out));
  Button button_153 (.out(button_153_out));
  Button button_154 (.out(button_154_out));
  Button button_155 (.out(button_155_out));
  Button button_156 (.out(button_156_out));
  Button button_157 (.out(button_157_out));
  Button button_158 (.out(button_158_out));
  Button button_159 (.out(button_159_out));
  Button button_160 (.out(button_160_out));
  Button button_161 (.out(button_161_out));
  Button button_162 (.out(button_162_out));
  Button button_163 (.out(button_163_out));
  Button button_164 (.out(button_164_out));
  Button button_165 (.out(button_165_out));
  Button button_166 (.out(button_166_out));
  Button button_167 (.out(button_167_out));
  Button button_168 (.out(button_168_out));
  Button button_169 (.out(button_169_out));
  Button button_170 (.out(button_170_out));
  Button button_171 (.out(button_171_out));
  Button button_172 (.out(button_172_out));
  Button button_173 (.out(button_173_out));
  Button button_174 (.out(button_174_out));
  Button button_175 (.out(button_175_out));
  Button button_176 (.out(button_176_out));
  Button button_177 (.out(button_177_out));
  Button button_178 (.out(button_178_out));
  Button button_179 (.out(button_179_out));
  Button button_180 (.out(button_180_out));
  Button button_181 (.out(button_181_out));
  Button button_182 (.out(button_182_out));
  Button button_183 (.out(button_183_out));
  Button button_184 (.out(button_184_out));
  Button button_185 (.out(button_185_out));
  Button button_186 (.out(button_186_out));
  Button button_187 (.out(button_187_out));
  Button button_188 (.out(button_188_out));
  Button button_189 (.out(button_189_out));
  Button button_190 (.out(button_190_out));
  Button button_191 (.out(button_191_out));
  Button button_192 (.out(button_192_out));
  Button button_193 (.out(button_193_out));
  Button button_194 (.out(button_194_out));
  Button button_195 (.out(button_195_out));
  Button button_196 (.out(button_196_out));
  Button button_197 (.out(button_197_out));
  Button button_198 (.out(button_198_out));
  Button button_199 (.out(button_199_out));
  Button button_200 (.out(button_200_out));
  Button button_201 (.out(button_201_out));
  Button button_202 (.out(button_202_out));
  Button button_203 (.out(button_203_out));
  Button button_204 (.out(button_204_out));
  Button button_205 (.out(button_205_out));
  Button button_206 (.out(button_206_out));
  Button button_207 (.out(button_207_out));
  Button button_208 (.out(button_208_out));
  Button button_209 (.out(button_209_out));
  Button button_210 (.out(button_210_out));
  Button button_211 (.out(button_211_out));
  Button button_212 (.out(button_212_out));
  Button button_213 (.out(button_213_out));
  Button button_214 (.out(button_214_out));
  Button button_215 (.out(button_215_out));
  Button button_216 (.out(button_216_out));
  Button button_217 (.out(button_217_out));
  Button button_218 (.out(button_218_out));
  Button button_219 (.out(button_219_out));
  Button button_220 (.out(button_220_out));
  Button button_221 (.out(button_221_out));
  Button button_222 (.out(button_222_out));
  Button button_223 (.out(button_223_out));
  Button button_224 (.out(button_224_out));
  Button button_225 (.out(button_225_out));
  Inputrow inputrow_1 (
    .out_16(inputrow_1_out_16), .in_1(button_2_out), .in_2(button_1_out), .in_3(button_3_out),
    .in_4(button_47_out), .in_5(button_46_out), .in_6(button_49_out), .in_7(button_48_out),
    .in_8(button_106_out), .in_9(button_109_out), .in_10(button_108_out), .in_11(button_107_out),
    .in_12(button_167_out), .in_13(button_166_out), .in_14(button_169_out), .in_15(button_168_out));
  Inputrow inputrow_2 (
    .out_16(inputrow_2_out_16), .in_1(button_6_out), .in_2(button_5_out), .in_3(button_4_out),
    .in_4(button_53_out), .in_5(button_50_out), .in_6(button_52_out), .in_7(button_51_out),
    .in_8(button_112_out), .in_9(button_110_out), .in_10(button_111_out), .in_11(button_113_out),
    .in_12(button_172_out), .in_13(button_173_out), .in_14(button_171_out), .in_15(button_170_out));
  Inputrow inputrow_3 (
    .out_16(inputrow_3_out_16), .in_1(button_7_out), .in_2(button_8_out), .in_3(button_9_out),
    .in_4(button_55_out), .in_5(button_57_out), .in_6(button_54_out), .in_7(button_56_out),
    .in_8(button_117_out), .in_9(button_116_out), .in_10(button_114_out), .in_11(button_115_out),
    .in_12(button_175_out), .in_13(button_177_out), .in_14(button_174_out), .in_15(button_176_out));
  Inputrow inputrow_4 (
    .out_16(inputrow_4_out_16), .in_1(button_12_out), .in_2(button_10_out), .in_3(button_11_out),
    .in_4(button_60_out), .in_5(button_58_out), .in_6(button_59_out), .in_7(button_61_out),
    .in_8(button_121_out), .in_9(button_118_out), .in_10(button_120_out), .in_11(button_119_out),
    .in_12(button_180_out), .in_13(button_179_out), .in_14(button_181_out), .in_15(button_178_out));
  Inputrow inputrow_5 (
    .out_16(inputrow_5_out_16), .in_1(button_14_out), .in_2(button_13_out), .in_3(button_15_out),
    .in_4(button_62_out), .in_5(button_64_out), .in_6(button_63_out), .in_7(button_65_out),
    .in_8(button_125_out), .in_9(button_123_out), .in_10(button_122_out), .in_11(button_124_out),
    .in_12(button_183_out), .in_13(button_185_out), .in_14(button_182_out), .in_15(button_184_out));
  Inputrow inputrow_6 (
    .out_16(inputrow_6_out_16), .in_1(button_17_out), .in_2(button_18_out), .in_3(button_16_out),
    .in_4(button_66_out), .in_5(button_67_out), .in_6(button_68_out), .in_7(button_69_out),
    .in_8(button_128_out), .in_9(button_126_out), .in_10(button_127_out), .in_11(button_129_out),
    .in_12(button_189_out), .in_13(button_187_out), .in_14(button_186_out), .in_15(button_188_out));
  Inputrow inputrow_7 (
    .out_16(inputrow_7_out_16), .in_1(button_20_out), .in_2(button_19_out), .in_3(button_21_out),
    .in_4(button_71_out), .in_5(button_73_out), .in_6(button_72_out), .in_7(button_70_out),
    .in_8(button_131_out), .in_9(button_132_out), .in_10(button_133_out), .in_11(button_130_out),
    .in_12(button_190_out), .in_13(button_192_out), .in_14(button_191_out), .in_15(button_193_out));
  Inputrow inputrow_8 (
    .out_16(inputrow_8_out_16), .in_1(button_23_out), .in_2(button_22_out), .in_3(button_24_out),
    .in_4(button_75_out), .in_5(button_74_out), .in_6(button_76_out), .in_7(button_77_out),
    .in_8(button_135_out), .in_9(button_136_out), .in_10(button_134_out), .in_11(button_137_out),
    .in_12(button_195_out), .in_13(button_196_out), .in_14(button_194_out), .in_15(button_197_out));
  Inputrow inputrow_9 (
    .out_16(inputrow_9_out_16), .in_1(button_27_out), .in_2(button_26_out), .in_3(button_25_out),
    .in_4(button_79_out), .in_5(button_80_out), .in_6(button_81_out), .in_7(button_78_out),
    .in_8(button_138_out), .in_9(button_141_out), .in_10(button_139_out), .in_11(button_140_out),
    .in_12(button_200_out), .in_13(button_201_out), .in_14(button_199_out), .in_15(button_198_out));
  Inputrow inputrow_10 (
    .out_16(inputrow_10_out_16), .in_1(button_28_out), .in_2(button_30_out), .in_3(button_29_out),
    .in_4(button_84_out), .in_5(button_85_out), .in_6(button_82_out), .in_7(button_83_out),
    .in_8(button_144_out), .in_9(button_143_out), .in_10(button_142_out), .in_11(button_145_out),
    .in_12(button_203_out), .in_13(button_202_out), .in_14(button_205_out), .in_15(button_204_out));
  Inputrow inputrow_11 (
    .out_16(inputrow_11_out_16), .in_1(button_33_out), .in_2(button_32_out), .in_3(button_31_out),
    .in_4(button_89_out), .in_5(button_87_out), .in_6(button_86_out), .in_7(button_88_out),
    .in_8(button_149_out), .in_9(button_146_out), .in_10(button_148_out), .in_11(button_147_out),
    .in_12(button_208_out), .in_13(button_206_out), .in_14(button_207_out), .in_15(button_209_out));
  Inputrow inputrow_12 (
    .out_16(inputrow_12_out_16), .in_1(button_36_out), .in_2(button_34_out), .in_3(button_35_out),
    .in_4(button_91_out), .in_5(button_92_out), .in_6(button_90_out), .in_7(button_93_out),
    .in_8(button_151_out), .in_9(button_152_out), .in_10(button_153_out), .in_11(button_150_out),
    .in_12(button_211_out), .in_13(button_212_out), .in_14(button_213_out), .in_15(button_210_out));
  Inputrow inputrow_13 (
    .out_16(inputrow_13_out_16), .in_1(button_38_out), .in_2(button_39_out), .in_3(button_37_out),
    .in_4(button_95_out), .in_5(button_97_out), .in_6(button_96_out), .in_7(button_94_out),
    .in_8(button_155_out), .in_9(button_154_out), .in_10(button_156_out), .in_11(button_157_out),
    .in_12(button_216_out), .in_13(button_217_out), .in_14(button_215_out), .in_15(button_214_out));
  Inputrow inputrow_14 (
    .out_16(inputrow_14_out_16), .in_1(button_41_out), .in_2(button_42_out), .in_3(button_40_out),
    .in_4(button_100_out), .in_5(button_98_out), .in_6(button_101_out), .in_7(button_99_out),
    .in_8(button_160_out), .in_9(button_158_out), .in_10(button_161_out), .in_11(button_159_out),
    .in_12(button_220_out), .in_13(button_218_out), .in_14(button_219_out), .in_15(button_221_out));
  Inputrow inputrow_15 (
    .out_16(inputrow_15_out_16), .in_1(button_45_out), .in_2(button_43_out), .in_3(button_44_out),
    .in_4(button_102_out), .in_5(button_103_out), .in_6(button_105_out), .in_7(button_104_out),
    .in_8(button_163_out), .in_9(button_165_out), .in_10(button_162_out), .in_11(button_164_out),
    .in_12(button_222_out), .in_13(button_225_out), .in_14(button_224_out), .in_15(button_223_out));
  Button Step (.out(Step_out));
  Clock clock_1 (.Run(Run__Attivare_Ticks_prima), .Step(Step_out), .out_3(clock_1_out_3));
  Force__l_utente_cambia_i_bit force_l_utente_cambia_i_bit_1 (
    .in_1(inputrow_1_out_16), .in_3(inputrow_2_out_16), .in_4(inputrow_3_out_16), .in_5(inputrow_4_out_16),
    .in_6(inputrow_5_out_16), .in_7(inputrow_6_out_16), .in_8(inputrow_7_out_16), .in_9(inputrow_8_out_16),
    .in_10(inputrow_9_out_16), .in_11(inputrow_10_out_16), .in_12(inputrow_11_out_16),
    .in_13(inputrow_12_out_16), .in_14(inputrow_13_out_16), .in_15(inputrow_14_out_16),
    .in_16(inputrow_15_out_16), .in_2(clock_1_out_3), .out_17(force_l_utente_cambia_i_bit_1_out_17),
    .out_18(force_l_utente_cambia_i_bit_1_out_18), .out_19(force_l_utente_cambia_i_bit_1_out_19),
    .out_20(force_l_utente_cambia_i_bit_1_out_20), .out_21(force_l_utente_cambia_i_bit_1_out_21),
    .out_22(force_l_utente_cambia_i_bit_1_out_22), .out_23(force_l_utente_cambia_i_bit_1_out_23),
    .out_24(force_l_utente_cambia_i_bit_1_out_24), .out_25(force_l_utente_cambia_i_bit_1_out_25),
    .out_26(force_l_utente_cambia_i_bit_1_out_26), .out_27(force_l_utente_cambia_i_bit_1_out_27),
    .out_28(force_l_utente_cambia_i_bit_1_out_28), .out_29(force_l_utente_cambia_i_bit_1_out_29),
    .out_30(force_l_utente_cambia_i_bit_1_out_30), .out_31(force_l_utente_cambia_i_bit_1_out_31));
  Counter #(.width(32), .max('hffffffff)) Counter (
    .Q(Counter_q), .clk(clock_1_out_3), .clr(setresetcounter_1_out_16));  // open: load, D, count, carry
  DotMatrix #(.inputtype("row"), .matrixcols(15), .matrixrows(15)) dotmatrix_1 (
    .row0(force_l_utente_cambia_i_bit_1_out_17), .row1(force_l_utente_cambia_i_bit_1_out_18),
    .row2(force_l_utente_cambia_i_bit_1_out_19), .row3(force_l_utente_cambia_i_bit_1_out_20),
    .row4(force_l_utente_cambia_i_bit_1_out_21), .row5(force_l_utente_cambia_i_bit_1_out_22),
    .row6(force_l_utente_cambia_i_bit_1_out_23), .row7(force_l_utente_cambia_i_bit_1_out_24),
    .row8(force_l_utente_cambia_i_bit_1_out_25), .row9(force_l_utente_cambia_i_bit_1_out_26),
    .row10(force_l_utente_cambia_i_bit_1_out_27), .row11(force_l_utente_cambia_i_bit_1_out_28),
    .row12(force_l_utente_cambia_i_bit_1_out_29), .row13(force_l_utente_cambia_i_bit_1_out_30),
    .row14(force_l_utente_cambia_i_bit_1_out_31));
  SetResetCounter setresetcounter_1 (
    .in_1(force_l_utente_cambia_i_bit_1_out_17), .in_2(force_l_utente_cambia_i_bit_1_out_18),
    .in_3(force_l_utente_cambia_i_bit_1_out_19), .in_4(force_l_utente_cambia_i_bit_1_out_20),
    .in_5(force_l_utente_cambia_i_bit_1_out_21), .in_6(force_l_utente_cambia_i_bit_1_out_22),
    .in_7(force_l_utente_cambia_i_bit_1_out_23), .in_8(force_l_utente_cambia_i_bit_1_out_24),
    .in_9(force_l_utente_cambia_i_bit_1_out_25), .in_10(force_l_utente_cambia_i_bit_1_out_26),
    .in_11(force_l_utente_cambia_i_bit_1_out_27), .in_12(force_l_utente_cambia_i_bit_1_out_28),
    .in_13(force_l_utente_cambia_i_bit_1_out_29), .in_14(force_l_utente_cambia_i_bit_1_out_30),
    .in_15(force_l_utente_cambia_i_bit_1_out_31), .out_16(setresetcounter_1_out_16));
  Register #(.width(32)) register_1 (.D(Counter_q), .Q(out_2), .clk(setresetcounter_1_out_16));  // open: en, clr
  // Probe on out_2

  // Notes on the sheet:
  //   The Game of Life
  //   Life toggler
  //   A
  //   B
  //   C
  //   Se il display della matrice
  //   ha dei pixel rossi d'errore,
  //   disattivare la simulazione (Ctrl+E).
  //   Poi riaprire il circuito.
endmodule

module Inputrow (
  input  in_1,
  input  in_2,
  input  in_3,
  input  in_4,
  input  in_5,
  input  in_6,
  input  in_7,
  input  in_8,
  input  in_9,
  input  in_10,
  input  in_11,
  input  in_12,
  input  in_13,
  input  in_14,
  input  in_15,
  output [14:0] out_16
);


  assign out_16 = {in_1, in_2, in_3, in_4, in_5, in_6, in_7, in_8, in_9, in_10, in_11, in_12, in_13, in_14, in_15};
endmodule

module Force__l_utente_cambia_i_bit (
  input  [14:0] in_1,
  input  in_2,
  input  [14:0] in_3,
  input  [14:0] in_4,
  input  [14:0] in_5,
  input  [14:0] in_6,
  input  [14:0] in_7,
  input  [14:0] in_8,
  input  [14:0] in_9,
  input  [14:0] in_10,
  input  [14:0] in_11,
  input  [14:0] in_12,
  input  [14:0] in_13,
  input  [14:0] in_14,
  input  [14:0] in_15,
  input  [14:0] in_16,
  output [14:0] out_17,
  output [14:0] out_18,
  output [14:0] out_19,
  output [14:0] out_20,
  output [14:0] out_21,
  output [14:0] out_22,
  output [14:0] out_23,
  output [14:0] out_24,
  output [14:0] out_25,
  output [14:0] out_26,
  output [14:0] out_27,
  output [14:0] out_28,
  output [14:0] out_29,
  output [14:0] out_30,
  output [14:0] out_31
);

  wire storage_row_1_out_48, storage_row_1_out_49, storage_row_1_out_50, storage_row_1_out_51,
       storage_row_1_out_52, storage_row_1_out_53, storage_row_1_out_54, storage_row_1_out_55,
       storage_row_1_out_56, storage_row_1_out_57, storage_row_1_out_58, storage_row_1_out_59,
       storage_row_1_out_60, storage_row_1_out_61, storage_row_1_out_62, storage_row_2_out_33,
       storage_row_2_out_34, storage_row_2_out_35, storage_row_2_out_36, storage_row_2_out_37,
       storage_row_2_out_38, storage_row_2_out_39, storage_row_2_out_40, storage_row_2_out_41,
       storage_row_2_out_42, storage_row_2_out_43, storage_row_2_out_44, storage_row_2_out_45,
       storage_row_2_out_46, storage_row_2_out_47, storage_row_2_out_48, storage_row_2_out_49,
       storage_row_2_out_50, storage_row_2_out_51, storage_row_2_out_52, storage_row_2_out_53,
       storage_row_2_out_54, storage_row_2_out_55, storage_row_2_out_56, storage_row_2_out_57,
       storage_row_2_out_58, storage_row_2_out_59, storage_row_2_out_60, storage_row_2_out_61,
       storage_row_2_out_62, storage_row_3_out_33, storage_row_3_out_34, storage_row_3_out_35,
       storage_row_3_out_36, storage_row_3_out_37, storage_row_3_out_38, storage_row_3_out_39,
       storage_row_3_out_40, storage_row_3_out_41, storage_row_3_out_42, storage_row_3_out_43,
       storage_row_3_out_44, storage_row_3_out_45, storage_row_3_out_46, storage_row_3_out_47,
       storage_row_3_out_48, storage_row_3_out_49, storage_row_3_out_50, storage_row_3_out_51,
       storage_row_3_out_52, storage_row_3_out_53, storage_row_3_out_54, storage_row_3_out_55,
       storage_row_3_out_56, storage_row_3_out_57, storage_row_3_out_58, storage_row_3_out_59,
       storage_row_3_out_60, storage_row_3_out_61, storage_row_3_out_62, storage_row_4_out_33,
       storage_row_4_out_34, storage_row_4_out_35, storage_row_4_out_36, storage_row_4_out_37,
       storage_row_4_out_38, storage_row_4_out_39, storage_row_4_out_40, storage_row_4_out_41,
       storage_row_4_out_42, storage_row_4_out_43, storage_row_4_out_44, storage_row_4_out_45,
       storage_row_4_out_46, storage_row_4_out_47, storage_row_4_out_48, storage_row_4_out_49,
       storage_row_4_out_50, storage_row_4_out_51, storage_row_4_out_52, storage_row_4_out_53,
       storage_row_4_out_54, storage_row_4_out_55, storage_row_4_out_56, storage_row_4_out_57,
       storage_row_4_out_58, storage_row_4_out_59, storage_row_4_out_60, storage_row_4_out_61,
       storage_row_4_out_62, storage_row_5_out_33, storage_row_5_out_34, storage_row_5_out_35,
       storage_row_5_out_36, storage_row_5_out_37, storage_row_5_out_38, storage_row_5_out_39,
       storage_row_5_out_40, storage_row_5_out_41, storage_row_5_out_42, storage_row_5_out_43,
       storage_row_5_out_44, storage_row_5_out_45, storage_row_5_out_46, storage_row_5_out_47,
       storage_row_5_out_48, storage_row_5_out_49, storage_row_5_out_50, storage_row_5_out_51,
       storage_row_5_out_52, storage_row_5_out_53, storage_row_5_out_54, storage_row_5_out_55,
       storage_row_5_out_56, storage_row_5_out_57, storage_row_5_out_58, storage_row_5_out_59,
       storage_row_5_out_60, storage_row_5_out_61, storage_row_5_out_62, storage_row_6_out_33,
       storage_row_6_out_34, storage_row_6_out_35, storage_row_6_out_36, storage_row_6_out_37,
       storage_row_6_out_38, storage_row_6_out_39, storage_row_6_out_40, storage_row_6_out_41,
       storage_row_6_out_42, storage_row_6_out_43, storage_row_6_out_44, storage_row_6_out_45,
       storage_row_6_out_46, storage_row_6_out_47, storage_row_6_out_48, storage_row_6_out_49,
       storage_row_6_out_50, storage_row_6_out_51, storage_row_6_out_52, storage_row_6_out_53,
       storage_row_6_out_54, storage_row_6_out_55, storage_row_6_out_56, storage_row_6_out_57,
       storage_row_6_out_58, storage_row_6_out_59, storage_row_6_out_60, storage_row_6_out_61,
       storage_row_6_out_62, storage_row_7_out_33, storage_row_7_out_34, storage_row_7_out_35,
       storage_row_7_out_36, storage_row_7_out_37, storage_row_7_out_38, storage_row_7_out_39,
       storage_row_7_out_40, storage_row_7_out_41, storage_row_7_out_42, storage_row_7_out_43,
       storage_row_7_out_44, storage_row_7_out_45, storage_row_7_out_46, storage_row_7_out_47,
       storage_row_7_out_48, storage_row_7_out_49, storage_row_7_out_50, storage_row_7_out_51,
       storage_row_7_out_52, storage_row_7_out_53, storage_row_7_out_54, storage_row_7_out_55,
       storage_row_7_out_56, storage_row_7_out_57, storage_row_7_out_58, storage_row_7_out_59,
       storage_row_7_out_60, storage_row_7_out_61, storage_row_7_out_62, storage_row_8_out_33,
       storage_row_8_out_34, storage_row_8_out_35, storage_row_8_out_36, storage_row_8_out_37,
       storage_row_8_out_38, storage_row_8_out_39, storage_row_8_out_40, storage_row_8_out_41,
       storage_row_8_out_42, storage_row_8_out_43, storage_row_8_out_44, storage_row_8_out_45,
       storage_row_8_out_46, storage_row_8_out_47, storage_row_8_out_48, storage_row_8_out_49,
       storage_row_8_out_50, storage_row_8_out_51, storage_row_8_out_52, storage_row_8_out_53,
       storage_row_8_out_54, storage_row_8_out_55, storage_row_8_out_56, storage_row_8_out_57,
       storage_row_8_out_58, storage_row_8_out_59, storage_row_8_out_60, storage_row_8_out_61,
       storage_row_8_out_62, storage_row_9_out_33, storage_row_9_out_34, storage_row_9_out_35,
       storage_row_9_out_36, storage_row_9_out_37, storage_row_9_out_38, storage_row_9_out_39,
       storage_row_9_out_40, storage_row_9_out_41, storage_row_9_out_42, storage_row_9_out_43,
       storage_row_9_out_44, storage_row_9_out_45, storage_row_9_out_46, storage_row_9_out_47,
       storage_row_9_out_48, storage_row_9_out_49, storage_row_9_out_50, storage_row_9_out_51,
       storage_row_9_out_52, storage_row_9_out_53, storage_row_9_out_54, storage_row_9_out_55,
       storage_row_9_out_56, storage_row_9_out_57, storage_row_9_out_58, storage_row_9_out_59,
       storage_row_9_out_60, storage_row_9_out_61, storage_row_9_out_62, storage_row_10_out_33,
       storage_row_10_out_34, storage_row_10_out_35, storage_row_10_out_36, storage_row_10_out_37,
       storage_row_10_out_38, storage_row_10_out_39, storage_row_10_out_40, storage_row_10_out_41,
       storage_row_10_out_42, storage_row_10_out_43, storage_row_10_out_44, storage_row_10_out_45,
       storage_row_10_out_46, storage_row_10_out_47, storage_row_10_out_48, storage_row_10_out_49,
       storage_row_10_out_50, storage_row_10_out_51, storage_row_10_out_52, storage_row_10_out_53,
       storage_row_10_out_54, storage_row_10_out_55, storage_row_10_out_56, storage_row_10_out_57,
       storage_row_10_out_58, storage_row_10_out_59, storage_row_10_out_60, storage_row_10_out_61,
       storage_row_10_out_62, storage_row_11_out_33, storage_row_11_out_34, storage_row_11_out_35,
       storage_row_11_out_36, storage_row_11_out_37, storage_row_11_out_38, storage_row_11_out_39,
       storage_row_11_out_40, storage_row_11_out_41, storage_row_11_out_42, storage_row_11_out_43,
       storage_row_11_out_44, storage_row_11_out_45, storage_row_11_out_46, storage_row_11_out_47,
       storage_row_11_out_48, storage_row_11_out_49, storage_row_11_out_50, storage_row_11_out_51,
       storage_row_11_out_52, storage_row_11_out_53, storage_row_11_out_54, storage_row_11_out_55,
       storage_row_11_out_56, storage_row_11_out_57, storage_row_11_out_58, storage_row_11_out_59,
       storage_row_11_out_60, storage_row_11_out_61, storage_row_11_out_62, storage_row_12_out_33,
       storage_row_12_out_34, storage_row_12_out_35, storage_row_12_out_36, storage_row_12_out_37,
       storage_row_12_out_38, storage_row_12_out_39, storage_row_12_out_40, storage_row_12_out_41,
       storage_row_12_out_42, storage_row_12_out_43, storage_row_12_out_44, storage_row_12_out_45,
       storage_row_12_out_46, storage_row_12_out_47, storage_row_12_out_48, storage_row_12_out_49,
       storage_row_12_out_50, storage_row_12_out_51, storage_row_12_out_52, storage_row_12_out_53,
       storage_row_12_out_54, storage_row_12_out_55, storage_row_12_out_56, storage_row_12_out_57,
       storage_row_12_out_58, storage_row_12_out_59, storage_row_12_out_60, storage_row_12_out_61,
       storage_row_12_out_62, storage_row_13_out_33, storage_row_13_out_34, storage_row_13_out_35,
       storage_row_13_out_36, storage_row_13_out_37, storage_row_13_out_38, storage_row_13_out_39,
       storage_row_13_out_40, storage_row_13_out_41, storage_row_13_out_42, storage_row_13_out_43,
       storage_row_13_out_44, storage_row_13_out_45, storage_row_13_out_46, storage_row_13_out_47,
       storage_row_13_out_48, storage_row_13_out_49, storage_row_13_out_50, storage_row_13_out_51,
       storage_row_13_out_52, storage_row_13_out_53, storage_row_13_out_54, storage_row_13_out_55,
       storage_row_13_out_56, storage_row_13_out_57, storage_row_13_out_58, storage_row_13_out_59,
       storage_row_13_out_60, storage_row_13_out_61, storage_row_13_out_62, storage_row_14_out_33,
       storage_row_14_out_34, storage_row_14_out_35, storage_row_14_out_36, storage_row_14_out_37,
       storage_row_14_out_38, storage_row_14_out_39, storage_row_14_out_40, storage_row_14_out_41,
       storage_row_14_out_42, storage_row_14_out_43, storage_row_14_out_44, storage_row_14_out_45,
       storage_row_14_out_46, storage_row_14_out_47, storage_row_14_out_48, storage_row_14_out_49,
       storage_row_14_out_50, storage_row_14_out_51, storage_row_14_out_52, storage_row_14_out_53,
       storage_row_14_out_54, storage_row_14_out_55, storage_row_14_out_56, storage_row_14_out_57,
       storage_row_14_out_58, storage_row_14_out_59, storage_row_14_out_60, storage_row_14_out_61,
       storage_row_14_out_62, storage_row_15_out_33, storage_row_15_out_34, storage_row_15_out_35,
       storage_row_15_out_36, storage_row_15_out_37, storage_row_15_out_38, storage_row_15_out_39,
       storage_row_15_out_40, storage_row_15_out_41, storage_row_15_out_42, storage_row_15_out_43,
       storage_row_15_out_44, storage_row_15_out_45, storage_row_15_out_46, storage_row_15_out_47,
       storage_row_16_out_33, storage_row_16_out_34, storage_row_16_out_35, storage_row_16_out_36,
       storage_row_16_out_37, storage_row_16_out_38, storage_row_16_out_39, storage_row_16_out_40,
       storage_row_16_out_41, storage_row_16_out_42, storage_row_16_out_43, storage_row_16_out_44,
       storage_row_16_out_45, storage_row_16_out_46, storage_row_16_out_47, storage_row_16_out_48,
       storage_row_16_out_49, undriven, undriven_3, undriven_4, undriven_5, undriven_6, undriven_7,
       undriven_8;
  wire [14:0] display_16_out_16, undriven_2;
  wire [29:0] storage_row_1_out_47;

  Storage_row storage_row_1 (
    .Clock(in_2), .Force(in_1), .in_1(storage_row_1_out_47[29]), .out_33(storage_row_1_out_47[28]),
    .in_2(storage_row_1_out_47[27]), .out_34(storage_row_1_out_47[26]), .in_3(storage_row_1_out_47[25]),
    .out_35(storage_row_1_out_47[24]), .in_4(storage_row_1_out_47[23]), .out_36(storage_row_1_out_47[22]),
    .in_5(storage_row_1_out_47[21]), .out_37(storage_row_1_out_47[20]), .in_6(storage_row_1_out_47[19]),
    .out_38(storage_row_1_out_47[18]), .in_7(storage_row_1_out_47[17]), .out_39(storage_row_1_out_47[16]),
    .in_8(storage_row_1_out_47[15]), .out_40(storage_row_1_out_47[14]), .in_9(storage_row_1_out_47[13]),
    .out_41(storage_row_1_out_47[12]), .in_10(storage_row_1_out_47[11]), .out_42(storage_row_1_out_47[10]),
    .in_11(storage_row_1_out_47[9]), .out_43(storage_row_1_out_47[8]), .in_12(storage_row_1_out_47[7]),
    .out_44(storage_row_1_out_47[6]), .in_13(storage_row_1_out_47[5]), .out_45(storage_row_1_out_47[4]),
    .in_14(storage_row_1_out_47[3]), .out_46(storage_row_1_out_47[2]), .in_15(storage_row_1_out_47[1]),
    .out_47(storage_row_1_out_47[0]), .out_48(storage_row_1_out_48), .in_17(storage_row_2_out_33),
    .out_49(storage_row_1_out_49), .in_18(storage_row_2_out_34), .out_50(storage_row_1_out_50),
    .in_19(storage_row_2_out_35), .out_51(storage_row_1_out_51), .in_20(storage_row_2_out_36),
    .out_52(storage_row_1_out_52), .in_21(storage_row_2_out_37), .out_53(storage_row_1_out_53),
    .in_22(storage_row_2_out_38), .out_54(storage_row_1_out_54), .in_23(storage_row_2_out_39),
    .out_55(storage_row_1_out_55), .in_24(storage_row_2_out_40), .out_56(storage_row_1_out_56),
    .in_25(storage_row_2_out_41), .out_57(storage_row_1_out_57), .in_26(storage_row_2_out_42),
    .out_58(storage_row_1_out_58), .in_27(storage_row_2_out_43), .out_59(storage_row_1_out_59),
    .in_28(storage_row_2_out_44), .out_60(storage_row_1_out_60), .in_29(storage_row_2_out_45),
    .out_61(storage_row_1_out_61), .in_30(storage_row_2_out_46), .out_62(storage_row_1_out_62),
    .in_31(storage_row_2_out_47));
  Storage_row storage_row_2 (
    .Clock(in_2), .Force(in_3), .in_1(storage_row_1_out_48), .out_33(storage_row_2_out_33),
    .in_2(storage_row_1_out_49), .out_34(storage_row_2_out_34), .in_3(storage_row_1_out_50),
    .out_35(storage_row_2_out_35), .in_4(storage_row_1_out_51), .out_36(storage_row_2_out_36),
    .in_5(storage_row_1_out_52), .out_37(storage_row_2_out_37), .in_6(storage_row_1_out_53),
    .out_38(storage_row_2_out_38), .in_7(storage_row_1_out_54), .out_39(storage_row_2_out_39),
    .in_8(storage_row_1_out_55), .out_40(storage_row_2_out_40), .in_9(storage_row_1_out_56),
    .out_41(storage_row_2_out_41), .in_10(storage_row_1_out_57), .out_42(storage_row_2_out_42),
    .in_11(storage_row_1_out_58), .out_43(storage_row_2_out_43), .in_12(storage_row_1_out_59),
    .out_44(storage_row_2_out_44), .in_13(storage_row_1_out_60), .out_45(storage_row_2_out_45),
    .in_14(storage_row_1_out_61), .out_46(storage_row_2_out_46), .in_15(storage_row_1_out_62),
    .out_47(storage_row_2_out_47), .out_48(storage_row_2_out_48), .in_17(storage_row_3_out_33),
    .out_49(storage_row_2_out_49), .in_18(storage_row_3_out_34), .out_50(storage_row_2_out_50),
    .in_19(storage_row_3_out_35), .out_51(storage_row_2_out_51), .in_20(storage_row_3_out_36),
    .out_52(storage_row_2_out_52), .in_21(storage_row_3_out_37), .out_53(storage_row_2_out_53),
    .in_22(storage_row_3_out_38), .out_54(storage_row_2_out_54), .in_23(storage_row_3_out_39),
    .out_55(storage_row_2_out_55), .in_24(storage_row_3_out_40), .out_56(storage_row_2_out_56),
    .in_25(storage_row_3_out_41), .out_57(storage_row_2_out_57), .in_26(storage_row_3_out_42),
    .out_58(storage_row_2_out_58), .in_27(storage_row_3_out_43), .out_59(storage_row_2_out_59),
    .in_28(storage_row_3_out_44), .out_60(storage_row_2_out_60), .in_29(storage_row_3_out_45),
    .out_61(storage_row_2_out_61), .in_30(storage_row_3_out_46), .out_62(storage_row_2_out_62),
    .in_31(storage_row_3_out_47));
  Storage_row storage_row_3 (
    .Clock(in_2), .Force(in_4), .in_1(storage_row_2_out_48), .out_33(storage_row_3_out_33),
    .in_2(storage_row_2_out_49), .out_34(storage_row_3_out_34), .in_3(storage_row_2_out_50),
    .out_35(storage_row_3_out_35), .in_4(storage_row_2_out_51), .out_36(storage_row_3_out_36),
    .in_5(storage_row_2_out_52), .out_37(storage_row_3_out_37), .in_6(storage_row_2_out_53),
    .out_38(storage_row_3_out_38), .in_7(storage_row_2_out_54), .out_39(storage_row_3_out_39),
    .in_8(storage_row_2_out_55), .out_40(storage_row_3_out_40), .in_9(storage_row_2_out_56),
    .out_41(storage_row_3_out_41), .in_10(storage_row_2_out_57), .out_42(storage_row_3_out_42),
    .in_11(storage_row_2_out_58), .out_43(storage_row_3_out_43), .in_12(storage_row_2_out_59),
    .out_44(storage_row_3_out_44), .in_13(storage_row_2_out_60), .out_45(storage_row_3_out_45),
    .in_14(storage_row_2_out_61), .out_46(storage_row_3_out_46), .in_15(storage_row_2_out_62),
    .out_47(storage_row_3_out_47), .out_48(storage_row_3_out_48), .in_17(storage_row_4_out_33),
    .out_49(storage_row_3_out_49), .in_18(storage_row_4_out_34), .out_50(storage_row_3_out_50),
    .in_19(storage_row_4_out_35), .out_51(storage_row_3_out_51), .in_20(storage_row_4_out_36),
    .out_52(storage_row_3_out_52), .in_21(storage_row_4_out_37), .out_53(storage_row_3_out_53),
    .in_22(storage_row_4_out_38), .out_54(storage_row_3_out_54), .in_23(storage_row_4_out_39),
    .out_55(storage_row_3_out_55), .in_24(storage_row_4_out_40), .out_56(storage_row_3_out_56),
    .in_25(storage_row_4_out_41), .out_57(storage_row_3_out_57), .in_26(storage_row_4_out_42),
    .out_58(storage_row_3_out_58), .in_27(storage_row_4_out_43), .out_59(storage_row_3_out_59),
    .in_28(storage_row_4_out_44), .out_60(storage_row_3_out_60), .in_29(storage_row_4_out_45),
    .out_61(storage_row_3_out_61), .in_30(storage_row_4_out_46), .out_62(storage_row_3_out_62),
    .in_31(storage_row_4_out_47));
  Storage_row storage_row_4 (
    .Clock(in_2), .Force(in_5), .in_1(storage_row_3_out_48), .out_33(storage_row_4_out_33),
    .in_2(storage_row_3_out_49), .out_34(storage_row_4_out_34), .in_3(storage_row_3_out_50),
    .out_35(storage_row_4_out_35), .in_4(storage_row_3_out_51), .out_36(storage_row_4_out_36),
    .in_5(storage_row_3_out_52), .out_37(storage_row_4_out_37), .in_6(storage_row_3_out_53),
    .out_38(storage_row_4_out_38), .in_7(storage_row_3_out_54), .out_39(storage_row_4_out_39),
    .in_8(storage_row_3_out_55), .out_40(storage_row_4_out_40), .in_9(storage_row_3_out_56),
    .out_41(storage_row_4_out_41), .in_10(storage_row_3_out_57), .out_42(storage_row_4_out_42),
    .in_11(storage_row_3_out_58), .out_43(storage_row_4_out_43), .in_12(storage_row_3_out_59),
    .out_44(storage_row_4_out_44), .in_13(storage_row_3_out_60), .out_45(storage_row_4_out_45),
    .in_14(storage_row_3_out_61), .out_46(storage_row_4_out_46), .in_15(storage_row_3_out_62),
    .out_47(storage_row_4_out_47), .out_48(storage_row_4_out_48), .in_17(storage_row_5_out_33),
    .out_49(storage_row_4_out_49), .in_18(storage_row_5_out_34), .out_50(storage_row_4_out_50),
    .in_19(storage_row_5_out_35), .out_51(storage_row_4_out_51), .in_20(storage_row_5_out_36),
    .out_52(storage_row_4_out_52), .in_21(storage_row_5_out_37), .out_53(storage_row_4_out_53),
    .in_22(storage_row_5_out_38), .out_54(storage_row_4_out_54), .in_23(storage_row_5_out_39),
    .out_55(storage_row_4_out_55), .in_24(storage_row_5_out_40), .out_56(storage_row_4_out_56),
    .in_25(storage_row_5_out_41), .out_57(storage_row_4_out_57), .in_26(storage_row_5_out_42),
    .out_58(storage_row_4_out_58), .in_27(storage_row_5_out_43), .out_59(storage_row_4_out_59),
    .in_28(storage_row_5_out_44), .out_60(storage_row_4_out_60), .in_29(storage_row_5_out_45),
    .out_61(storage_row_4_out_61), .in_30(storage_row_5_out_46), .out_62(storage_row_4_out_62),
    .in_31(storage_row_5_out_47));
  Storage_row storage_row_5 (
    .Clock(in_2), .Force(in_6), .in_1(storage_row_4_out_48), .out_33(storage_row_5_out_33),
    .in_2(storage_row_4_out_49), .out_34(storage_row_5_out_34), .in_3(storage_row_4_out_50),
    .out_35(storage_row_5_out_35), .in_4(storage_row_4_out_51), .out_36(storage_row_5_out_36),
    .in_5(storage_row_4_out_52), .out_37(storage_row_5_out_37), .in_6(storage_row_4_out_53),
    .out_38(storage_row_5_out_38), .in_7(storage_row_4_out_54), .out_39(storage_row_5_out_39),
    .in_8(storage_row_4_out_55), .out_40(storage_row_5_out_40), .in_9(storage_row_4_out_56),
    .out_41(storage_row_5_out_41), .in_10(storage_row_4_out_57), .out_42(storage_row_5_out_42),
    .in_11(storage_row_4_out_58), .out_43(storage_row_5_out_43), .in_12(storage_row_4_out_59),
    .out_44(storage_row_5_out_44), .in_13(storage_row_4_out_60), .out_45(storage_row_5_out_45),
    .in_14(storage_row_4_out_61), .out_46(storage_row_5_out_46), .in_15(storage_row_4_out_62),
    .out_47(storage_row_5_out_47), .out_48(storage_row_5_out_48), .in_17(storage_row_6_out_33),
    .out_49(storage_row_5_out_49), .in_18(storage_row_6_out_34), .out_50(storage_row_5_out_50),
    .in_19(storage_row_6_out_35), .out_51(storage_row_5_out_51), .in_20(storage_row_6_out_36),
    .out_52(storage_row_5_out_52), .in_21(storage_row_6_out_37), .out_53(storage_row_5_out_53),
    .in_22(storage_row_6_out_38), .out_54(storage_row_5_out_54), .in_23(storage_row_6_out_39),
    .out_55(storage_row_5_out_55), .in_24(storage_row_6_out_40), .out_56(storage_row_5_out_56),
    .in_25(storage_row_6_out_41), .out_57(storage_row_5_out_57), .in_26(storage_row_6_out_42),
    .out_58(storage_row_5_out_58), .in_27(storage_row_6_out_43), .out_59(storage_row_5_out_59),
    .in_28(storage_row_6_out_44), .out_60(storage_row_5_out_60), .in_29(storage_row_6_out_45),
    .out_61(storage_row_5_out_61), .in_30(storage_row_6_out_46), .out_62(storage_row_5_out_62),
    .in_31(storage_row_6_out_47));
  Storage_row storage_row_6 (
    .Clock(in_2), .Force(in_7), .in_1(storage_row_5_out_48), .out_33(storage_row_6_out_33),
    .in_2(storage_row_5_out_49), .out_34(storage_row_6_out_34), .in_3(storage_row_5_out_50),
    .out_35(storage_row_6_out_35), .in_4(storage_row_5_out_51), .out_36(storage_row_6_out_36),
    .in_5(storage_row_5_out_52), .out_37(storage_row_6_out_37), .in_6(storage_row_5_out_53),
    .out_38(storage_row_6_out_38), .in_7(storage_row_5_out_54), .out_39(storage_row_6_out_39),
    .in_8(storage_row_5_out_55), .out_40(storage_row_6_out_40), .in_9(storage_row_5_out_56),
    .out_41(storage_row_6_out_41), .in_10(storage_row_5_out_57), .out_42(storage_row_6_out_42),
    .in_11(storage_row_5_out_58), .out_43(storage_row_6_out_43), .in_12(storage_row_5_out_59),
    .out_44(storage_row_6_out_44), .in_13(storage_row_5_out_60), .out_45(storage_row_6_out_45),
    .in_14(storage_row_5_out_61), .out_46(storage_row_6_out_46), .in_15(storage_row_5_out_62),
    .out_47(storage_row_6_out_47), .out_48(storage_row_6_out_48), .in_17(storage_row_7_out_33),
    .out_49(storage_row_6_out_49), .in_18(storage_row_7_out_34), .out_50(storage_row_6_out_50),
    .in_19(storage_row_7_out_35), .out_51(storage_row_6_out_51), .in_20(storage_row_7_out_36),
    .out_52(storage_row_6_out_52), .in_21(storage_row_7_out_37), .out_53(storage_row_6_out_53),
    .in_22(storage_row_7_out_38), .out_54(storage_row_6_out_54), .in_23(storage_row_7_out_39),
    .out_55(storage_row_6_out_55), .in_24(storage_row_7_out_40), .out_56(storage_row_6_out_56),
    .in_25(storage_row_7_out_41), .out_57(storage_row_6_out_57), .in_26(storage_row_7_out_42),
    .out_58(storage_row_6_out_58), .in_27(storage_row_7_out_43), .out_59(storage_row_6_out_59),
    .in_28(storage_row_7_out_44), .out_60(storage_row_6_out_60), .in_29(storage_row_7_out_45),
    .out_61(storage_row_6_out_61), .in_30(storage_row_7_out_46), .out_62(storage_row_6_out_62),
    .in_31(storage_row_7_out_47));
  Storage_row storage_row_7 (
    .Clock(in_2), .Force(in_8), .in_1(storage_row_6_out_48), .out_33(storage_row_7_out_33),
    .in_2(storage_row_6_out_49), .out_34(storage_row_7_out_34), .in_3(storage_row_6_out_50),
    .out_35(storage_row_7_out_35), .in_4(storage_row_6_out_51), .out_36(storage_row_7_out_36),
    .in_5(storage_row_6_out_52), .out_37(storage_row_7_out_37), .in_6(storage_row_6_out_53),
    .out_38(storage_row_7_out_38), .in_7(storage_row_6_out_54), .out_39(storage_row_7_out_39),
    .in_8(storage_row_6_out_55), .out_40(storage_row_7_out_40), .in_9(storage_row_6_out_56),
    .out_41(storage_row_7_out_41), .in_10(storage_row_6_out_57), .out_42(storage_row_7_out_42),
    .in_11(storage_row_6_out_58), .out_43(storage_row_7_out_43), .in_12(storage_row_6_out_59),
    .out_44(storage_row_7_out_44), .in_13(storage_row_6_out_60), .out_45(storage_row_7_out_45),
    .in_14(storage_row_6_out_61), .out_46(storage_row_7_out_46), .in_15(storage_row_6_out_62),
    .out_47(storage_row_7_out_47), .out_48(storage_row_7_out_48), .in_17(storage_row_8_out_33),
    .out_49(storage_row_7_out_49), .in_18(storage_row_8_out_34), .out_50(storage_row_7_out_50),
    .in_19(storage_row_8_out_35), .out_51(storage_row_7_out_51), .in_20(storage_row_8_out_36),
    .out_52(storage_row_7_out_52), .in_21(storage_row_8_out_37), .out_53(storage_row_7_out_53),
    .in_22(storage_row_8_out_38), .out_54(storage_row_7_out_54), .in_23(storage_row_8_out_39),
    .out_55(storage_row_7_out_55), .in_24(storage_row_8_out_40), .out_56(storage_row_7_out_56),
    .in_25(storage_row_8_out_41), .out_57(storage_row_7_out_57), .in_26(storage_row_8_out_42),
    .out_58(storage_row_7_out_58), .in_27(storage_row_8_out_43), .out_59(storage_row_7_out_59),
    .in_28(storage_row_8_out_44), .out_60(storage_row_7_out_60), .in_29(storage_row_8_out_45),
    .out_61(storage_row_7_out_61), .in_30(storage_row_8_out_46), .out_62(storage_row_7_out_62),
    .in_31(storage_row_8_out_47));
  Storage_row storage_row_8 (
    .Clock(in_2), .Force(in_9), .in_1(storage_row_7_out_48), .out_33(storage_row_8_out_33),
    .in_2(storage_row_7_out_49), .out_34(storage_row_8_out_34), .in_3(storage_row_7_out_50),
    .out_35(storage_row_8_out_35), .in_4(storage_row_7_out_51), .out_36(storage_row_8_out_36),
    .in_5(storage_row_7_out_52), .out_37(storage_row_8_out_37), .in_6(storage_row_7_out_53),
    .out_38(storage_row_8_out_38), .in_7(storage_row_7_out_54), .out_39(storage_row_8_out_39),
    .in_8(storage_row_7_out_55), .out_40(storage_row_8_out_40), .in_9(storage_row_7_out_56),
    .out_41(storage_row_8_out_41), .in_10(storage_row_7_out_57), .out_42(storage_row_8_out_42),
    .in_11(storage_row_7_out_58), .out_43(storage_row_8_out_43), .in_12(storage_row_7_out_59),
    .out_44(storage_row_8_out_44), .in_13(storage_row_7_out_60), .out_45(storage_row_8_out_45),
    .in_14(storage_row_7_out_61), .out_46(storage_row_8_out_46), .in_15(storage_row_7_out_62),
    .out_47(storage_row_8_out_47), .out_48(storage_row_8_out_48), .in_17(storage_row_9_out_33),
    .out_49(storage_row_8_out_49), .in_18(storage_row_9_out_34), .out_50(storage_row_8_out_50),
    .in_19(storage_row_9_out_35), .out_51(storage_row_8_out_51), .in_20(storage_row_9_out_36),
    .out_52(storage_row_8_out_52), .in_21(storage_row_9_out_37), .out_53(storage_row_8_out_53),
    .in_22(storage_row_9_out_38), .out_54(storage_row_8_out_54), .in_23(storage_row_9_out_39),
    .out_55(storage_row_8_out_55), .in_24(storage_row_9_out_40), .out_56(storage_row_8_out_56),
    .in_25(storage_row_9_out_41), .out_57(storage_row_8_out_57), .in_26(storage_row_9_out_42),
    .out_58(storage_row_8_out_58), .in_27(storage_row_9_out_43), .out_59(storage_row_8_out_59),
    .in_28(storage_row_9_out_44), .out_60(storage_row_8_out_60), .in_29(storage_row_9_out_45),
    .out_61(storage_row_8_out_61), .in_30(storage_row_9_out_46), .out_62(storage_row_8_out_62),
    .in_31(storage_row_9_out_47));
  Storage_row storage_row_9 (
    .Clock(in_2), .Force(in_10), .in_1(storage_row_8_out_48), .out_33(storage_row_9_out_33),
    .in_2(storage_row_8_out_49), .out_34(storage_row_9_out_34), .in_3(storage_row_8_out_50),
    .out_35(storage_row_9_out_35), .in_4(storage_row_8_out_51), .out_36(storage_row_9_out_36),
    .in_5(storage_row_8_out_52), .out_37(storage_row_9_out_37), .in_6(storage_row_8_out_53),
    .out_38(storage_row_9_out_38), .in_7(storage_row_8_out_54), .out_39(storage_row_9_out_39),
    .in_8(storage_row_8_out_55), .out_40(storage_row_9_out_40), .in_9(storage_row_8_out_56),
    .out_41(storage_row_9_out_41), .in_10(storage_row_8_out_57), .out_42(storage_row_9_out_42),
    .in_11(storage_row_8_out_58), .out_43(storage_row_9_out_43), .in_12(storage_row_8_out_59),
    .out_44(storage_row_9_out_44), .in_13(storage_row_8_out_60), .out_45(storage_row_9_out_45),
    .in_14(storage_row_8_out_61), .out_46(storage_row_9_out_46), .in_15(storage_row_8_out_62),
    .out_47(storage_row_9_out_47), .out_48(storage_row_9_out_48), .in_17(storage_row_10_out_33),
    .out_49(storage_row_9_out_49), .in_18(storage_row_10_out_34), .out_50(storage_row_9_out_50),
    .in_19(storage_row_10_out_35), .out_51(storage_row_9_out_51), .in_20(storage_row_10_out_36),
    .out_52(storage_row_9_out_52), .in_21(storage_row_10_out_37), .out_53(storage_row_9_out_53),
    .in_22(storage_row_10_out_38), .out_54(storage_row_9_out_54), .in_23(storage_row_10_out_39),
    .out_55(storage_row_9_out_55), .in_24(storage_row_10_out_40), .out_56(storage_row_9_out_56),
    .in_25(storage_row_10_out_41), .out_57(storage_row_9_out_57), .in_26(storage_row_10_out_42),
    .out_58(storage_row_9_out_58), .in_27(storage_row_10_out_43), .out_59(storage_row_9_out_59),
    .in_28(storage_row_10_out_44), .out_60(storage_row_9_out_60), .in_29(storage_row_10_out_45),
    .out_61(storage_row_9_out_61), .in_30(storage_row_10_out_46), .out_62(storage_row_9_out_62),
    .in_31(storage_row_10_out_47));
  Storage_row storage_row_10 (
    .Clock(in_2), .Force(in_11), .in_1(storage_row_9_out_48), .out_33(storage_row_10_out_33),
    .in_2(storage_row_9_out_49), .out_34(storage_row_10_out_34), .in_3(storage_row_9_out_50),
    .out_35(storage_row_10_out_35), .in_4(storage_row_9_out_51), .out_36(storage_row_10_out_36),
    .in_5(storage_row_9_out_52), .out_37(storage_row_10_out_37), .in_6(storage_row_9_out_53),
    .out_38(storage_row_10_out_38), .in_7(storage_row_9_out_54), .out_39(storage_row_10_out_39),
    .in_8(storage_row_9_out_55), .out_40(storage_row_10_out_40), .in_9(storage_row_9_out_56),
    .out_41(storage_row_10_out_41), .in_10(storage_row_9_out_57), .out_42(storage_row_10_out_42),
    .in_11(storage_row_9_out_58), .out_43(storage_row_10_out_43), .in_12(storage_row_9_out_59),
    .out_44(storage_row_10_out_44), .in_13(storage_row_9_out_60), .out_45(storage_row_10_out_45),
    .in_14(storage_row_9_out_61), .out_46(storage_row_10_out_46), .in_15(storage_row_9_out_62),
    .out_47(storage_row_10_out_47), .out_48(storage_row_10_out_48), .in_17(storage_row_11_out_33),
    .out_49(storage_row_10_out_49), .in_18(storage_row_11_out_34), .out_50(storage_row_10_out_50),
    .in_19(storage_row_11_out_35), .out_51(storage_row_10_out_51), .in_20(storage_row_11_out_36),
    .out_52(storage_row_10_out_52), .in_21(storage_row_11_out_37), .out_53(storage_row_10_out_53),
    .in_22(storage_row_11_out_38), .out_54(storage_row_10_out_54), .in_23(storage_row_11_out_39),
    .out_55(storage_row_10_out_55), .in_24(storage_row_11_out_40), .out_56(storage_row_10_out_56),
    .in_25(storage_row_11_out_41), .out_57(storage_row_10_out_57), .in_26(storage_row_11_out_42),
    .out_58(storage_row_10_out_58), .in_27(storage_row_11_out_43), .out_59(storage_row_10_out_59),
    .in_28(storage_row_11_out_44), .out_60(storage_row_10_out_60), .in_29(storage_row_11_out_45),
    .out_61(storage_row_10_out_61), .in_30(storage_row_11_out_46), .out_62(storage_row_10_out_62),
    .in_31(storage_row_11_out_47));
  Storage_row storage_row_11 (
    .Clock(in_2), .Force(in_12), .in_1(storage_row_10_out_48), .out_33(storage_row_11_out_33),
    .in_2(storage_row_10_out_49), .out_34(storage_row_11_out_34), .in_3(storage_row_10_out_50),
    .out_35(storage_row_11_out_35), .in_4(storage_row_10_out_51), .out_36(storage_row_11_out_36),
    .in_5(storage_row_10_out_52), .out_37(storage_row_11_out_37), .in_6(storage_row_10_out_53),
    .out_38(storage_row_11_out_38), .in_7(storage_row_10_out_54), .out_39(storage_row_11_out_39),
    .in_8(storage_row_10_out_55), .out_40(storage_row_11_out_40), .in_9(storage_row_10_out_56),
    .out_41(storage_row_11_out_41), .in_10(storage_row_10_out_57), .out_42(storage_row_11_out_42),
    .in_11(storage_row_10_out_58), .out_43(storage_row_11_out_43), .in_12(storage_row_10_out_59),
    .out_44(storage_row_11_out_44), .in_13(storage_row_10_out_60), .out_45(storage_row_11_out_45),
    .in_14(storage_row_10_out_61), .out_46(storage_row_11_out_46), .in_15(storage_row_10_out_62),
    .out_47(storage_row_11_out_47), .out_48(storage_row_11_out_48), .in_17(storage_row_12_out_33),
    .out_49(storage_row_11_out_49), .in_18(storage_row_12_out_34), .out_50(storage_row_11_out_50),
    .in_19(storage_row_12_out_35), .out_51(storage_row_11_out_51), .in_20(storage_row_12_out_36),
    .out_52(storage_row_11_out_52), .in_21(storage_row_12_out_37), .out_53(storage_row_11_out_53),
    .in_22(storage_row_12_out_38), .out_54(storage_row_11_out_54), .in_23(storage_row_12_out_39),
    .out_55(storage_row_11_out_55), .in_24(storage_row_12_out_40), .out_56(storage_row_11_out_56),
    .in_25(storage_row_12_out_41), .out_57(storage_row_11_out_57), .in_26(storage_row_12_out_42),
    .out_58(storage_row_11_out_58), .in_27(storage_row_12_out_43), .out_59(storage_row_11_out_59),
    .in_28(storage_row_12_out_44), .out_60(storage_row_11_out_60), .in_29(storage_row_12_out_45),
    .out_61(storage_row_11_out_61), .in_30(storage_row_12_out_46), .out_62(storage_row_11_out_62),
    .in_31(storage_row_12_out_47));
  Storage_row storage_row_12 (
    .Clock(in_2), .Force(in_13), .in_1(storage_row_11_out_48), .out_33(storage_row_12_out_33),
    .in_2(storage_row_11_out_49), .out_34(storage_row_12_out_34), .in_3(storage_row_11_out_50),
    .out_35(storage_row_12_out_35), .in_4(storage_row_11_out_51), .out_36(storage_row_12_out_36),
    .in_5(storage_row_11_out_52), .out_37(storage_row_12_out_37), .in_6(storage_row_11_out_53),
    .out_38(storage_row_12_out_38), .in_7(storage_row_11_out_54), .out_39(storage_row_12_out_39),
    .in_8(storage_row_11_out_55), .out_40(storage_row_12_out_40), .in_9(storage_row_11_out_56),
    .out_41(storage_row_12_out_41), .in_10(storage_row_11_out_57), .out_42(storage_row_12_out_42),
    .in_11(storage_row_11_out_58), .out_43(storage_row_12_out_43), .in_12(storage_row_11_out_59),
    .out_44(storage_row_12_out_44), .in_13(storage_row_11_out_60), .out_45(storage_row_12_out_45),
    .in_14(storage_row_11_out_61), .out_46(storage_row_12_out_46), .in_15(storage_row_11_out_62),
    .out_47(storage_row_12_out_47), .out_48(storage_row_12_out_48), .in_17(storage_row_13_out_33),
    .out_49(storage_row_12_out_49), .in_18(storage_row_13_out_34), .out_50(storage_row_12_out_50),
    .in_19(storage_row_13_out_35), .out_51(storage_row_12_out_51), .in_20(storage_row_13_out_36),
    .out_52(storage_row_12_out_52), .in_21(storage_row_13_out_37), .out_53(storage_row_12_out_53),
    .in_22(storage_row_13_out_38), .out_54(storage_row_12_out_54), .in_23(storage_row_13_out_39),
    .out_55(storage_row_12_out_55), .in_24(storage_row_13_out_40), .out_56(storage_row_12_out_56),
    .in_25(storage_row_13_out_41), .out_57(storage_row_12_out_57), .in_26(storage_row_13_out_42),
    .out_58(storage_row_12_out_58), .in_27(storage_row_13_out_43), .out_59(storage_row_12_out_59),
    .in_28(storage_row_13_out_44), .out_60(storage_row_12_out_60), .in_29(storage_row_13_out_45),
    .out_61(storage_row_12_out_61), .in_30(storage_row_13_out_46), .out_62(storage_row_12_out_62),
    .in_31(storage_row_13_out_47));
  Storage_row storage_row_13 (
    .Clock(in_2), .Force(in_14), .in_1(storage_row_12_out_48), .out_33(storage_row_13_out_33),
    .in_2(storage_row_12_out_49), .out_34(storage_row_13_out_34), .in_3(storage_row_12_out_50),
    .out_35(storage_row_13_out_35), .in_4(storage_row_12_out_51), .out_36(storage_row_13_out_36),
    .in_5(storage_row_12_out_52), .out_37(storage_row_13_out_37), .in_6(storage_row_12_out_53),
    .out_38(storage_row_13_out_38), .in_7(storage_row_12_out_54), .out_39(storage_row_13_out_39),
    .in_8(storage_row_12_out_55), .out_40(storage_row_13_out_40), .in_9(storage_row_12_out_56),
    .out_41(storage_row_13_out_41), .in_10(storage_row_12_out_57), .out_42(storage_row_13_out_42),
    .in_11(storage_row_12_out_58), .out_43(storage_row_13_out_43), .in_12(storage_row_12_out_59),
    .out_44(storage_row_13_out_44), .in_13(storage_row_12_out_60), .out_45(storage_row_13_out_45),
    .in_14(storage_row_12_out_61), .out_46(storage_row_13_out_46), .in_15(storage_row_12_out_62),
    .out_47(storage_row_13_out_47), .out_48(storage_row_13_out_48), .in_17(storage_row_14_out_33),
    .out_49(storage_row_13_out_49), .in_18(storage_row_14_out_34), .out_50(storage_row_13_out_50),
    .in_19(storage_row_14_out_35), .out_51(storage_row_13_out_51), .in_20(storage_row_14_out_36),
    .out_52(storage_row_13_out_52), .in_21(storage_row_14_out_37), .out_53(storage_row_13_out_53),
    .in_22(storage_row_14_out_38), .out_54(storage_row_13_out_54), .in_23(storage_row_14_out_39),
    .out_55(storage_row_13_out_55), .in_24(storage_row_14_out_40), .out_56(storage_row_13_out_56),
    .in_25(storage_row_14_out_41), .out_57(storage_row_13_out_57), .in_26(storage_row_14_out_42),
    .out_58(storage_row_13_out_58), .in_27(storage_row_14_out_43), .out_59(storage_row_13_out_59),
    .in_28(storage_row_14_out_44), .out_60(storage_row_13_out_60), .in_29(storage_row_14_out_45),
    .out_61(storage_row_13_out_61), .in_30(storage_row_14_out_46), .out_62(storage_row_13_out_62),
    .in_31(storage_row_14_out_47));
  Storage_row storage_row_14 (
    .Clock(in_2), .Force(in_15), .in_1(storage_row_13_out_48), .out_33(storage_row_14_out_33),
    .in_2(storage_row_13_out_49), .out_34(storage_row_14_out_34), .in_3(storage_row_13_out_50),
    .out_35(storage_row_14_out_35), .in_4(storage_row_13_out_51), .out_36(storage_row_14_out_36),
    .in_5(storage_row_13_out_52), .out_37(storage_row_14_out_37), .in_6(storage_row_13_out_53),
    .out_38(storage_row_14_out_38), .in_7(storage_row_13_out_54), .out_39(storage_row_14_out_39),
    .in_8(storage_row_13_out_55), .out_40(storage_row_14_out_40), .in_9(storage_row_13_out_56),
    .out_41(storage_row_14_out_41), .in_10(storage_row_13_out_57), .out_42(storage_row_14_out_42),
    .in_11(storage_row_13_out_58), .out_43(storage_row_14_out_43), .in_12(storage_row_13_out_59),
    .out_44(storage_row_14_out_44), .in_13(storage_row_13_out_60), .out_45(storage_row_14_out_45),
    .in_14(storage_row_13_out_61), .out_46(storage_row_14_out_46), .in_15(storage_row_13_out_62),
    .out_47(storage_row_14_out_47), .out_48(storage_row_14_out_48), .in_17(storage_row_15_out_33),
    .out_49(storage_row_14_out_49), .in_18(storage_row_15_out_34), .out_50(storage_row_14_out_50),
    .in_19(storage_row_15_out_35), .out_51(storage_row_14_out_51), .in_20(storage_row_15_out_36),
    .out_52(storage_row_14_out_52), .in_21(storage_row_15_out_37), .out_53(storage_row_14_out_53),
    .in_22(storage_row_15_out_38), .out_54(storage_row_14_out_54), .in_23(storage_row_15_out_39),
    .out_55(storage_row_14_out_55), .in_24(storage_row_15_out_40), .out_56(storage_row_14_out_56),
    .in_25(storage_row_15_out_41), .out_57(storage_row_14_out_57), .in_26(storage_row_15_out_42),
    .out_58(storage_row_14_out_58), .in_27(storage_row_15_out_43), .out_59(storage_row_14_out_59),
    .in_28(storage_row_15_out_44), .out_60(storage_row_14_out_60), .in_29(storage_row_15_out_45),
    .out_61(storage_row_14_out_61), .in_30(storage_row_15_out_46), .out_62(storage_row_14_out_62),
    .in_31(storage_row_15_out_47));
  Storage_row storage_row_15 (
    .Clock(in_2), .Force(in_16), .in_1(storage_row_14_out_48), .out_33(storage_row_15_out_33),
    .in_2(storage_row_14_out_49), .out_34(storage_row_15_out_34), .in_3(storage_row_14_out_50),
    .out_35(storage_row_15_out_35), .in_4(storage_row_14_out_51), .out_36(storage_row_15_out_36),
    .in_5(storage_row_14_out_52), .out_37(storage_row_15_out_37), .in_6(storage_row_14_out_53),
    .out_38(storage_row_15_out_38), .in_7(storage_row_14_out_54), .out_39(storage_row_15_out_39),
    .in_8(storage_row_14_out_55), .out_40(storage_row_15_out_40), .in_9(storage_row_14_out_56),
    .out_41(storage_row_15_out_41), .in_10(storage_row_14_out_57), .out_42(storage_row_15_out_42),
    .in_11(storage_row_14_out_58), .out_43(storage_row_15_out_43), .in_12(storage_row_14_out_59),
    .out_44(storage_row_15_out_44), .in_13(storage_row_14_out_60), .out_45(storage_row_15_out_45),
    .in_14(storage_row_14_out_61), .out_46(storage_row_15_out_46), .in_15(storage_row_14_out_62),
    .out_47(storage_row_15_out_47), .out_48(storage_row_1_out_47[29]), .in_17(storage_row_1_out_47[28]),
    .out_49(storage_row_1_out_47[27]), .in_18(storage_row_1_out_47[26]), .out_50(storage_row_1_out_47[25]),
    .in_19(storage_row_1_out_47[24]), .out_51(storage_row_1_out_47[23]), .in_20(storage_row_1_out_47[22]),
    .out_52(storage_row_1_out_47[21]), .in_21(storage_row_1_out_47[20]), .out_53(storage_row_1_out_47[19]),
    .in_22(storage_row_1_out_47[18]), .out_54(storage_row_1_out_47[17]), .in_23(storage_row_1_out_47[16]),
    .out_55(storage_row_1_out_47[15]), .in_24(storage_row_1_out_47[14]), .out_56(storage_row_1_out_47[13]),
    .in_25(storage_row_1_out_47[12]), .out_57(storage_row_1_out_47[11]), .in_26(storage_row_1_out_47[10]),
    .out_58(storage_row_1_out_47[9]), .in_27(storage_row_1_out_47[8]), .out_59(storage_row_1_out_47[7]),
    .in_28(storage_row_1_out_47[6]), .out_60(storage_row_1_out_47[5]), .in_29(storage_row_1_out_47[4]),
    .out_61(storage_row_1_out_47[3]), .in_30(storage_row_1_out_47[2]), .out_62(storage_row_1_out_47[1]),
    .in_31(storage_row_1_out_47[0]));
  Display display_1 (
    .out_16(out_17), .in_1(storage_row_1_out_47[28]), .in_2(storage_row_1_out_47[26]),
    .in_3(storage_row_1_out_47[24]), .in_4(storage_row_1_out_47[22]), .in_5(storage_row_1_out_47[20]),
    .in_6(storage_row_1_out_47[18]), .in_7(storage_row_1_out_47[16]), .in_8(storage_row_1_out_47[14]),
    .in_9(storage_row_1_out_47[12]), .in_10(storage_row_1_out_47[10]), .in_11(storage_row_1_out_47[8]),
    .in_12(storage_row_1_out_47[6]), .in_13(storage_row_1_out_47[4]), .in_14(storage_row_1_out_47[2]),
    .in_15(storage_row_1_out_47[0]));
  Display display_2 (
    .out_16(out_18), .in_1(storage_row_2_out_33), .in_2(storage_row_2_out_34), .in_3(storage_row_2_out_35),
    .in_4(storage_row_2_out_36), .in_5(storage_row_2_out_37), .in_6(storage_row_2_out_38),
    .in_7(storage_row_2_out_39), .in_8(storage_row_2_out_40), .in_9(storage_row_2_out_41),
    .in_10(storage_row_2_out_42), .in_11(storage_row_2_out_43), .in_12(storage_row_2_out_44),
    .in_13(storage_row_2_out_45), .in_14(storage_row_2_out_46), .in_15(storage_row_2_out_47));
  Display display_3 (
    .out_16(out_19), .in_1(storage_row_3_out_33), .in_2(storage_row_3_out_34), .in_3(storage_row_3_out_35),
    .in_4(storage_row_3_out_36), .in_5(storage_row_3_out_37), .in_6(storage_row_3_out_38),
    .in_7(storage_row_3_out_39), .in_8(storage_row_3_out_40), .in_9(storage_row_3_out_41),
    .in_10(storage_row_3_out_42), .in_11(storage_row_3_out_43), .in_12(storage_row_3_out_44),
    .in_13(storage_row_3_out_45), .in_14(storage_row_3_out_46), .in_15(storage_row_3_out_47));
  Display display_4 (
    .out_16(out_20), .in_1(storage_row_4_out_33), .in_2(storage_row_4_out_34), .in_3(storage_row_4_out_35),
    .in_4(storage_row_4_out_36), .in_5(storage_row_4_out_37), .in_6(storage_row_4_out_38),
    .in_7(storage_row_4_out_39), .in_8(storage_row_4_out_40), .in_9(storage_row_4_out_41),
    .in_10(storage_row_4_out_42), .in_11(storage_row_4_out_43), .in_12(storage_row_4_out_44),
    .in_13(storage_row_4_out_45), .in_14(storage_row_4_out_46), .in_15(storage_row_4_out_47));
  Display display_5 (
    .out_16(out_21), .in_1(storage_row_5_out_33), .in_2(storage_row_5_out_34), .in_3(storage_row_5_out_35),
    .in_4(storage_row_5_out_36), .in_5(storage_row_5_out_37), .in_6(storage_row_5_out_38),
    .in_7(storage_row_5_out_39), .in_8(storage_row_5_out_40), .in_9(storage_row_5_out_41),
    .in_10(storage_row_5_out_42), .in_11(storage_row_5_out_43), .in_12(storage_row_5_out_44),
    .in_13(storage_row_5_out_45), .in_14(storage_row_5_out_46), .in_15(storage_row_5_out_47));
  Display display_6 (
    .out_16(out_22), .in_1(storage_row_6_out_33), .in_2(storage_row_6_out_34), .in_3(storage_row_6_out_35),
    .in_4(storage_row_6_out_36), .in_5(storage_row_6_out_37), .in_6(storage_row_6_out_38),
    .in_7(storage_row_6_out_39), .in_8(storage_row_6_out_40), .in_9(storage_row_6_out_41),
    .in_10(storage_row_6_out_42), .in_11(storage_row_6_out_43), .in_12(storage_row_6_out_44),
    .in_13(storage_row_6_out_45), .in_14(storage_row_6_out_46), .in_15(storage_row_6_out_47));
  Display display_7 (
    .out_16(out_23), .in_1(storage_row_7_out_33), .in_2(storage_row_7_out_34), .in_3(storage_row_7_out_35),
    .in_4(storage_row_7_out_36), .in_5(storage_row_7_out_37), .in_6(storage_row_7_out_38),
    .in_7(storage_row_7_out_39), .in_8(storage_row_7_out_40), .in_9(storage_row_7_out_41),
    .in_10(storage_row_7_out_42), .in_11(storage_row_7_out_43), .in_12(storage_row_7_out_44),
    .in_13(storage_row_7_out_45), .in_14(storage_row_7_out_46), .in_15(storage_row_7_out_47));
  Display display_8 (
    .out_16(out_24), .in_1(storage_row_8_out_33), .in_2(storage_row_8_out_34), .in_3(storage_row_8_out_35),
    .in_4(storage_row_8_out_36), .in_5(storage_row_8_out_37), .in_6(storage_row_8_out_38),
    .in_7(storage_row_8_out_39), .in_8(storage_row_8_out_40), .in_9(storage_row_8_out_41),
    .in_10(storage_row_8_out_42), .in_11(storage_row_8_out_43), .in_12(storage_row_8_out_44),
    .in_13(storage_row_8_out_45), .in_14(storage_row_8_out_46), .in_15(storage_row_8_out_47));
  Display display_9 (
    .out_16(out_25), .in_1(storage_row_9_out_33), .in_2(storage_row_9_out_34), .in_3(storage_row_9_out_35),
    .in_4(storage_row_9_out_36), .in_5(storage_row_9_out_37), .in_6(storage_row_9_out_38),
    .in_7(storage_row_9_out_39), .in_8(storage_row_9_out_40), .in_9(storage_row_9_out_41),
    .in_10(storage_row_9_out_42), .in_11(storage_row_9_out_43), .in_12(storage_row_9_out_44),
    .in_13(storage_row_9_out_45), .in_14(storage_row_9_out_46), .in_15(storage_row_9_out_47));
  Display display_10 (
    .out_16(out_26), .in_1(storage_row_10_out_33), .in_2(storage_row_10_out_34),
    .in_3(storage_row_10_out_35), .in_4(storage_row_10_out_36), .in_5(storage_row_10_out_37),
    .in_6(storage_row_10_out_38), .in_7(storage_row_10_out_39), .in_8(storage_row_10_out_40),
    .in_9(storage_row_10_out_41), .in_10(storage_row_10_out_42), .in_11(storage_row_10_out_43),
    .in_12(storage_row_10_out_44), .in_13(storage_row_10_out_45), .in_14(storage_row_10_out_46),
    .in_15(storage_row_10_out_47));
  Display display_11 (
    .out_16(out_27), .in_1(storage_row_11_out_33), .in_2(storage_row_11_out_34),
    .in_3(storage_row_11_out_35), .in_4(storage_row_11_out_36), .in_5(storage_row_11_out_37),
    .in_6(storage_row_11_out_38), .in_7(storage_row_11_out_39), .in_8(storage_row_11_out_40),
    .in_9(storage_row_11_out_41), .in_10(storage_row_11_out_42), .in_11(storage_row_11_out_43),
    .in_12(storage_row_11_out_44), .in_13(storage_row_11_out_45), .in_14(storage_row_11_out_46),
    .in_15(storage_row_11_out_47));
  Display display_12 (
    .out_16(out_28), .in_1(storage_row_12_out_33), .in_2(storage_row_12_out_34),
    .in_3(storage_row_12_out_35), .in_4(storage_row_12_out_36), .in_5(storage_row_12_out_37),
    .in_6(storage_row_12_out_38), .in_7(storage_row_12_out_39), .in_8(storage_row_12_out_40),
    .in_9(storage_row_12_out_41), .in_10(storage_row_12_out_42), .in_11(storage_row_12_out_43),
    .in_12(storage_row_12_out_44), .in_13(storage_row_12_out_45), .in_14(storage_row_12_out_46),
    .in_15(storage_row_12_out_47));
  Display display_13 (
    .out_16(out_29), .in_1(storage_row_13_out_33), .in_2(storage_row_13_out_34),
    .in_3(storage_row_13_out_35), .in_4(storage_row_13_out_36), .in_5(storage_row_13_out_37),
    .in_6(storage_row_13_out_38), .in_7(storage_row_13_out_39), .in_8(storage_row_13_out_40),
    .in_9(storage_row_13_out_41), .in_10(storage_row_13_out_42), .in_11(storage_row_13_out_43),
    .in_12(storage_row_13_out_44), .in_13(storage_row_13_out_45), .in_14(storage_row_13_out_46),
    .in_15(storage_row_13_out_47));
  Display display_14 (
    .out_16(out_30), .in_1(storage_row_14_out_33), .in_2(storage_row_14_out_34),
    .in_3(storage_row_14_out_35), .in_4(storage_row_14_out_36), .in_5(storage_row_14_out_37),
    .in_6(storage_row_14_out_38), .in_7(storage_row_14_out_39), .in_8(storage_row_14_out_40),
    .in_9(storage_row_14_out_41), .in_10(storage_row_14_out_42), .in_11(storage_row_14_out_43),
    .in_12(storage_row_14_out_44), .in_13(storage_row_14_out_45), .in_14(storage_row_14_out_46),
    .in_15(storage_row_14_out_47));
  Display display_15 (
    .out_16(out_31), .in_1(storage_row_15_out_33), .in_2(storage_row_15_out_34),
    .in_3(storage_row_15_out_35), .in_4(storage_row_15_out_36), .in_5(storage_row_15_out_37),
    .in_6(storage_row_15_out_38), .in_7(storage_row_15_out_39), .in_8(storage_row_15_out_40),
    .in_9(storage_row_15_out_41), .in_10(storage_row_15_out_42), .in_11(storage_row_15_out_43),
    .in_12(storage_row_15_out_44), .in_13(storage_row_15_out_45), .in_14(storage_row_15_out_46),
    .in_15(storage_row_15_out_47));
  Storage_row storage_row_16 (
    .Clock(undriven), .Force(undriven_2), .out_33(storage_row_16_out_33), .out_34(storage_row_16_out_34),
    .out_35(storage_row_16_out_35), .out_36(storage_row_16_out_36), .out_37(storage_row_16_out_37),
    .out_38(storage_row_16_out_38), .out_39(storage_row_16_out_39), .out_40(storage_row_16_out_40),
    .out_41(storage_row_16_out_41), .out_42(storage_row_16_out_42), .out_43(storage_row_16_out_43),
    .out_44(storage_row_16_out_44), .out_45(storage_row_16_out_45), .in_14(undriven_5),
    .out_46(storage_row_16_out_46), .in_15(undriven_7), .out_47(storage_row_16_out_47),
    .out_48(storage_row_16_out_48), .out_49(storage_row_16_out_49), .in_28(undriven_3), .in_29(undriven_4),
    .in_30(undriven_6), .in_31(undriven_8));  // open: in_1, in_2, in_3, in_4, in_5, in_6, in_7, in_8, in_9, in_10, in_11, in_12, in_13, in_17, in_18, out_50, in_19, out_51, in_20, out_52, in_21, out_53, in_22, out_54, in_23, out_55, in_24, out_56, in_25, out_57, in_26, out_58, in_27, out_59, out_60, out_61, out_62
  Display display_16 (
    .out_16(display_16_out_16), .in_1(storage_row_16_out_33), .in_2(storage_row_16_out_34),
    .in_3(storage_row_16_out_35), .in_4(storage_row_16_out_36), .in_5(storage_row_16_out_37),
    .in_6(storage_row_16_out_38), .in_7(storage_row_16_out_39), .in_8(storage_row_16_out_40),
    .in_9(storage_row_16_out_41), .in_10(storage_row_16_out_42), .in_11(storage_row_16_out_43),
    .in_12(storage_row_16_out_44), .in_13(storage_row_16_out_45), .in_14(storage_row_16_out_46),
    .in_15(storage_row_16_out_47));

  // Notes on the sheet:
  //   Clock
  //   Force (user switches bit)
  //   Output state to row above this one
  //   Output state to row below this one
  //   SCHEMA STORAGE
  //   Input states of row below this one
  //   To Display
  //   Input states of row above this one
  //   Stores & calcs curr state, updates on clock
endmodule

module Display (
  input  in_1,
  input  in_2,
  input  in_3,
  input  in_4,
  input  in_5,
  input  in_6,
  input  in_7,
  input  in_8,
  input  in_9,
  input  in_10,
  input  in_11,
  input  in_12,
  input  in_13,
  input  in_14,
  input  in_15,
  output [14:0] out_16
);


  assign out_16 = {in_1, in_2, in_3, in_4, in_5, in_6, in_7, in_8, in_9, in_10, in_11, in_12, in_13, in_14, in_15};
endmodule

module Storage_row (
  input  in_1,
  input  in_2,
  input  in_3,
  input  in_4,
  input  in_5,
  input  in_6,
  input  in_7,
  input  in_8,
  input  in_9,
  input  in_10,
  input  in_11,
  input  in_12,
  input  in_13,
  input  in_14,
  input  in_15,
  input  Clock,
  input  in_17,
  input  in_18,
  input  in_19,
  input  in_20,
  input  in_21,
  input  in_22,
  input  in_23,
  input  in_24,
  input  in_25,
  input  in_26,
  input  in_27,
  input  in_28,
  input  in_29,
  input  in_30,
  input  in_31,
  input  [14:0] Force,
  output out_33,
  output out_34,
  output out_35,
  output out_36,
  output out_37,
  output out_38,
  output out_39,
  output out_40,
  output out_41,
  output out_42,
  output out_43,
  output out_44,
  output out_45,
  output out_46,
  output out_47,
  output out_48,
  output out_49,
  output out_50,
  output out_51,
  output out_52,
  output out_53,
  output out_54,
  output out_55,
  output out_56,
  output out_57,
  output out_58,
  output out_59,
  output out_60,
  output out_61,
  output out_62
);

  wire new_1_current_3, new_1_current_4, new_2_current_3, new_2_current_4, new_3_current_3, new_3_current_4,
       new_4_current_3, new_4_current_4, new_5_current_3, new_5_current_4, new_6_current_3, new_6_current_4,
       new_7_current_3, new_7_current_4, new_8_current_3, new_8_current_4, new_9_current, new_9_current_2,
       new_9_current_3, new_9_current_4, new_10_current_3, new_10_current_4, new_11_current_3,
       new_11_current_4, new_12_current_3, new_12_current_4, new_13_current_3, new_13_current_4,
       new_14_current_3, new_14_current_4, new_15_current_3, new_15_current_4, new_16_current_3,
       new_16_current_4, undriven, undriven_2, undriven_3, undriven_4, undriven_5, undriven_6, undriven_7,
       undriven_8;

  New new_1 (
    .Current_3(new_1_current_3), .in_1(in_1), .in_2(new_2_current_4), .in_3(in_17), .in_4(new_16_current_3),
    .Force(Force[14]), .Clock(Clock), .Current_4(new_1_current_4), .Current(out_33), .Current_2(out_48),
    .in_7(in_2), .in_8(in_15), .in_9(in_18), .in_10(in_31));
  New new_2 (
    .Current_3(new_2_current_3), .in_1(in_2), .in_2(new_3_current_4), .in_3(in_18), .in_4(new_1_current_3),
    .Force(Force[13]), .Clock(Clock), .Current_4(new_2_current_4), .Current(out_34), .Current_2(out_49),
    .in_7(in_3), .in_8(in_1), .in_9(in_19), .in_10(in_17));
  New new_3 (
    .Current_3(new_3_current_3), .in_1(in_3), .in_2(new_5_current_4), .in_3(in_19), .in_4(new_2_current_3),
    .Force(Force[12]), .Clock(Clock), .Current_4(new_3_current_4), .Current(out_35), .Current_2(out_50),
    .in_7(in_4), .in_8(in_2), .in_9(in_20), .in_10(in_18));
  New new_4 (
    .Current_3(new_4_current_3), .in_1(in_5), .in_2(new_6_current_4), .in_3(in_21), .in_4(new_5_current_3),
    .Force(Force[10]), .Clock(Clock), .Current_4(new_4_current_4), .Current(out_37), .Current_2(out_52),
    .in_7(in_6), .in_8(in_4), .in_9(in_22), .in_10(in_20));
  New new_5 (
    .Current_3(new_5_current_3), .in_1(in_4), .in_2(new_4_current_4), .in_3(in_20), .in_4(new_3_current_3),
    .Force(Force[11]), .Clock(Clock), .Current_4(new_5_current_4), .Current(out_36), .Current_2(out_51),
    .in_7(in_5), .in_8(in_3), .in_9(in_21), .in_10(in_19));
  New new_6 (
    .Current_3(new_6_current_3), .in_1(in_6), .in_2(new_7_current_4), .in_3(in_22), .in_4(new_4_current_3),
    .Force(Force[9]), .Clock(Clock), .Current_4(new_6_current_4), .Current(out_38), .Current_2(out_53),
    .in_7(in_7), .in_8(in_5), .in_9(in_23), .in_10(in_21));
  New new_7 (
    .Current_3(new_7_current_3), .in_1(in_7), .in_2(new_8_current_4), .in_3(in_23), .in_4(new_6_current_3),
    .Force(Force[8]), .Clock(Clock), .Current_4(new_7_current_4), .Current(out_39), .Current_2(out_54),
    .in_7(in_8), .in_8(in_6), .in_9(in_24), .in_10(in_22));
  New new_8 (
    .Current_3(new_8_current_3), .in_1(in_8), .in_2(new_10_current_4), .in_3(in_24), .in_4(new_7_current_3),
    .Force(Force[7]), .Clock(Clock), .Current_4(new_8_current_4), .Current(out_40), .Current_2(out_55),
    .in_7(in_9), .in_8(in_7), .in_9(in_25), .in_10(in_23));
  New new_9 (
    .Current_3(new_9_current_3), .in_1(undriven_2), .in_2(undriven_8), .in_3(undriven_5), .in_4(undriven),
    .Current_4(new_9_current_4), .Current(new_9_current), .Current_2(new_9_current_2), .in_7(undriven_6),
    .in_8(undriven_3), .in_9(undriven_7), .in_10(undriven_4));  // open: Force, Clock
  New new_10 (
    .Current_3(new_10_current_3), .in_1(in_9), .in_2(new_11_current_4), .in_3(in_25), .in_4(new_8_current_3),
    .Force(Force[6]), .Clock(Clock), .Current_4(new_10_current_4), .Current(out_41), .Current_2(out_56),
    .in_7(in_10), .in_8(in_8), .in_9(in_26), .in_10(in_24));
  New new_11 (
    .Current_3(new_11_current_3), .in_1(in_10), .in_2(new_12_current_4), .in_3(in_26),
    .in_4(new_10_current_3), .Force(Force[5]), .Clock(Clock), .Current_4(new_11_current_4), .Current(out_42),
    .Current_2(out_57), .in_7(in_11), .in_8(in_9), .in_9(in_27), .in_10(in_25));
  New new_12 (
    .Current_3(new_12_current_3), .in_1(in_11), .in_2(new_13_current_4), .in_3(in_27),
    .in_4(new_11_current_3), .Force(Force[4]), .Clock(Clock), .Current_4(new_12_current_4), .Current(out_43),
    .Current_2(out_58), .in_7(in_12), .in_8(in_10), .in_9(in_28), .in_10(in_26));
  New new_13 (
    .Current_3(new_13_current_3), .in_1(in_12), .in_2(new_14_current_4), .in_3(in_28),
    .in_4(new_12_current_3), .Force(Force[3]), .Clock(Clock), .Current_4(new_13_current_4), .Current(out_44),
    .Current_2(out_59), .in_7(in_13), .in_8(in_11), .in_9(in_29), .in_10(in_27));
  New new_14 (
    .Current_3(new_14_current_3), .in_1(in_13), .in_2(new_15_current_4), .in_3(in_29),
    .in_4(new_13_current_3), .Force(Force[2]), .Clock(Clock), .Current_4(new_14_current_4), .Current(out_45),
    .Current_2(out_60), .in_7(in_14), .in_8(in_12), .in_9(in_30), .in_10(in_28));
  New new_15 (
    .Current_3(new_15_current_3), .in_1(in_14), .in_2(new_16_current_4), .in_3(in_30),
    .in_4(new_14_current_3), .Force(Force[1]), .Clock(Clock), .Current_4(new_15_current_4), .Current(out_46),
    .Current_2(out_61), .in_7(in_15), .in_8(in_13), .in_9(in_31), .in_10(in_29));
  New new_16 (
    .Current_3(new_16_current_3), .in_1(in_15), .in_2(new_1_current_4), .in_3(in_31),
    .in_4(new_15_current_3), .Force(Force[0]), .Clock(Clock), .Current_4(new_16_current_4), .Current(out_47),
    .Current_2(out_62), .in_7(in_1), .in_8(in_14), .in_9(in_17), .in_10(in_30));

  // Other names for the same wires on the sheet: BL = in_17; BR = in_31; TL = in_1; TR = in_15

  // Notes on the sheet:
  //   Output's current state
  //   Input's top state
  //   Input's top left state
  //   Input's left state
  //   Input's bottom left state
  //   Output's current state
  //   Output's current state
  //   SCHEMA STORAGE ROW
  //   Input's top right state
  //   Input's right state
  //   Output's current state
  //   Input's bottom right state
  //   Input's bottom right state
endmodule

module New (
  input  in_1,
  input  in_2,
  input  in_3,
  input  in_4,
  input  Force,
  input  Clock,
  input  in_7,
  input  in_8,
  input  in_9,
  input  in_10,
  output Current,
  output Current_2,
  output Current_3,
  output Current_4
);

  wire and_1_out, n2_or_3_1_three, n2_or_3_1_two, or_1_out;
  wire [1:0] adder_1_out, adder_2_out, adder_3_out, adder_4_out, adder_5_out, adder_6_out, adder_7_out;

  Adder #(.width(1)) adder_1 (.a(in_4), .b(in_3), .out(adder_1_out[0]), .cout(adder_1_out[1]));  // open: cin
  Adder #(.width(1)) adder_2 (.a(in_2), .b(in_1), .out(adder_2_out[0]), .cout(adder_2_out[1]));  // open: cin
  Adder #(.width(1)) adder_3 (.a(in_10), .b(in_9), .out(adder_3_out[0]), .cout(adder_3_out[1]));  // open: cin
  Adder #(.width(1)) adder_4 (.a(in_8), .b(in_7), .out(adder_4_out[0]), .cout(adder_4_out[1]));  // open: cin
  Adder #(.width(2)) adder_5 (.a(adder_1_out), .b(adder_2_out), .out(adder_5_out));  // open: cin, cout
  Adder #(.width(2)) adder_6 (.a(adder_3_out), .b(adder_4_out), .out(adder_6_out));  // open: cin, cout
  Adder #(.width(2)) adder_7 (.a(adder_5_out), .b(adder_6_out), .out(adder_7_out));  // open: cin, cout
  _2_or_3 u_2_or_3_1 (.in_1(adder_7_out[0]), .in_2(adder_7_out[1]), .Three(n2_or_3_1_three), .Two(n2_or_3_1_two));
  Current current_1 (.Current(Current), .New(or_1_out), .Clock(Clock), .Force(Force));
  or or_1 (or_1_out, n2_or_3_1_three, and_1_out);
  and and_1 (and_1_out, n2_or_3_1_two, Current);

  assign Current_2 = Current;
  assign Current_3 = Current;
  assign Current_4 = Current;

  // Notes on the sheet:
  //   Status of Neighbours
  //   Status of Neighbours
  //   True if sum of neighbours is 3 or 2 and the current is on
  //   Updates on clock, is switched on Force
endmodule

module Current (
  input  New,
  input  Clock,
  input  Force,
  output Current
);

  wire and_1_out, and_2_out, not_1_out, not_2_out, or_1_out, or_2_out;

  not not_1 (not_1_out, Force);
  and and_1 (and_1_out, not_2_out, Force);
  or or_1 (or_1_out, and_1_out, and_2_out);
  and and_2 (and_2_out, not_1_out, New);
  or or_2 (or_2_out, Force, Clock);
  not not_2 (not_2_out, Current);
  Register #(.width(1), .trigger("falling")) register_1 (.D(or_1_out), .Q(Current), .clk(or_2_out));  // open: en, clr
endmodule

module _2_or_3 (
  input  in_1,
  input  in_2,
  output Three,
  output Two
);

  wire not_1_out;

  not not_1 (not_1_out, in_1);
  and and_1 (Three, in_1, in_2);
  and and_2 (Two, not_1_out, in_2);
endmodule

module Clock (
  input  Run,
  input  Step,
  output out_3
);

  wire and_1_out, clock_1_out;

  and and_1 (and_1_out, Run, clock_1_out);
  Clock_part clock_1 (.out(clock_1_out));
  or or_1 (out_3, and_1_out, Step);
endmodule

module SetResetCounter (
  input  [14:0] in_1,
  input  [14:0] in_2,
  input  [14:0] in_3,
  input  [14:0] in_4,
  input  [14:0] in_5,
  input  [14:0] in_6,
  input  [14:0] in_7,
  input  [14:0] in_8,
  input  [14:0] in_9,
  input  [14:0] in_10,
  input  [14:0] in_11,
  input  [14:0] in_12,
  input  [14:0] in_13,
  input  [14:0] in_14,
  input  [14:0] in_15,
  output out_16
);

  wire [14:0] and_1_out;

  assign and_1_out = ~in_1 & ~in_2 & ~in_3 & ~in_4 & ~in_5 & ~in_6 & ~in_7 & ~in_8 & ~in_9 & ~in_10 & ~in_11 & ~in_12 & ~in_13 & ~in_14 & ~in_15;  // AND_Gate and_1, 15 bits wide
  Comparator #(.width(15)) comparator_1 (.a(and_1_out), .b({15{1'b1}}), .eq(out_16));  // open: gt, lt
endmodule
